// Logisim project main.circ as structural Verilog: 14 circuits, main circuit main
module main (
);

  wire _1onInp, _2onInp, _3onInp, _4onInp, _5onInp, adder_1_out, and_1_out, and_2_out, and_3_out, and_4_out,
       and_5_out, and_6_out, and_7_out, and_8_out, and_9_out, and_10_out, and_11_out, and_12_out, and_13_out,
       and_14_out, and_15_out, and_17_out, and_18_out, and_19_out, and_20_out, and_21_out, and_22_out,
       and_23_out, and_24_out, and_25_out, and_26_out, and_27_out, and_28_out, and_29_out, and_30_out,
       and_31_out, and_33_out, and_34_out, and_35_out, and_37_out, and_39_out, and_40_out, and_41_out,
       and_42_out, and_44_out, and_45_out, and_48_out, AonInp, ATCcorrectINP, ATCenMove, ATCenMoved,
       ATCinisW, ATCinit, ATCInpFlpre, ATCnEhp, ATCnewENclc, ATCplAttaked, ATCplLOSE, ATCplWIN, buffer_1_out,
       buffer_3_out, buffer_4_out, button_1_out, button_2_out, changePCx, changePCy, chGM, CHHPinmove,
       clock_1_out, comparator_1_eq, comparator_2_lt, comparator_3_gt, comparator_4_lt, comparator_5_gt,
       comparator_6_lt, comparator_7_gt, comparator_8_lt, comparator_9_gt, comparator_10_lt,
       comparator_11_gt, comparator_14_lt, comparator_15_gt, comparator_16_lt, comparator_17_gt,
       comparator_18_eq, comparator_19_eq, comparator_20_eq, comparator_21_eq, comparator_22_eq,
       comparator_22_gt, comparator_22_lt, comparator_23_eq, comparator_24_eq, comparator_25_eq,
       comparator_26_eq, comparator_27_eq, comparator_28_eq, comparator_29_eq, comparator_30_eq,
       comparator_31_eq, comparator_32_eq, comparator_33_eq, comparator_34_eq, comparator_35_eq,
       comparator_36_eq, comparator_37_eq, comparator_38_eq, comparator_39_eq, comparator_40_eq,
       comparator_41_eq, comparator_42_eq, comparator_43_eq, comparator_44_eq, comparator_45_lt,
       comparator_46_gt, comparator_47_lt, comparator_48_gt, comparator_49_lt, comparator_50_gt,
       comparator_51_lt, comparator_52_gt, comparator_53_lt, comparator_54_gt, comparator_63_eq,
       comparator_64_eq, comparator_65_eq, comparator_66_eq, comparator_67_eq, comparator_68_gt,
       comparator_69_gt, comparator_70_gt, comparator_71_gt, comparator_72_eq, comparator_72_lt,
       comparator_73_lt, comparator_74_lt, comparator_75_lt, comparator_76_lt, comparator_77_eq,
       CONSOLE_PRINTER_connected, demultiplexer_1_out1, demultiplexer_3_out0, demultiplexer_3_out1,
       demultiplexer_3_out2, demultiplexer_3_out3, demultiplexer_4_out0, demultiplexer_4_out1,
       demultiplexer_4_out2, DonInp, gS0, gS1, gS2, InpFl1, InpFl2, InpFlpreC, InpFlpreSTRT, INV1ch, INV2ch,
       INV3ch, INV4ch, INV5ch, invchn, ITEMinCELL, itemRES1, itemRES2, itemRES3, itemRES4, itemRES5,
       letsPrint, LoadMap, mainClk, mainRES, MapLevelCh, mapPREst, mapPREst1, memReadyToPrint, MOVEenHERE,
       MOVEinited, not_1_out, not_2_out, not_3_out, not_4_out, not_5_out, not_6_out, not_7_out, not_8_out,
       not_9_out, not_10_out, not_11_out, not_12_out, not_13_out, not_15_out, not_16_out, or_1_out, or_2_out,
       or_3_out, or_4_out, or_5_out, or_8_out, or_9_out, or_11_out, or_13_out, or_14_out, or_15_out,
       or_16_out, or_17_out, or_20_out, or_23_out, or_25_out, or_26_out, or_28_out, or_29_out,
       PlayerDeathRes, PLAYERHPCH, PlDirCh, printing_map_1_cond_of_change, pull_resistor_3_node,
       pull_resistor_4_node, pull_resistor_6_node, pull_resistor_9_node, qres, quick_1_out, quick_2_out,
       quick_8_out, quick_14_out, quick_15_out, quick_16_out, quick_17_out, quick_18_out, quick_20_out,
       quick_22_out, quick_23_out, quick_28_out, quick_29_out, quick_32_out, quick_33_out, random_1_out,
       register_6_q, StateCh, stMapCLC, stMapCLC1, stMapCLC2, WalkProcessed, WonInp, xor_1_out;
  wire [1:0] adder_12_out, ATCcurEN, ATCnewEN, bit_extender_4_out, bit_extender_5_out, bit_extender_6_out,
       bit_extender_7_out, gameState, gSto, NewPlDir, PlDir, subtractor_15_out;
  wire [2:0] bit_extender_1_out, bit_extender_3_out;
  wire [3:0] adder_4_out, register_13_q;
  wire [7:0] adder_2_out, adder_3_out, adder_5_out, adder_6_out, adder_7_out, adder_8_out, adder_10_out,
       adder_11_out, ATCInpKey, bit_extender_2_out, ENDMG, ENDMGst, enemies_1_hp, ENHP, ENHPst, ENimgChrst,
       ENIMN, ENNmChrst, food_1_givehp, graphic_elems_1_data, gStdtScrMem, InpKey, InpKeyall, INVENTORY1,
       INVENTORY1p, INVENTORY2, INVENTORY2p, INVENTORY3, INVENTORY3p, INVENTORY4, INVENTORY4p, INVENTORY5,
       INVENTORY5p, LENHP, mapLevelCur, maps_1_p3, maps_1_p5, mapSTDATAreaded, memChar, multiplexer_1_out,
       multiplexer_2_out, multiplexer_3_out, multiplexer_5_out, multiplexer_7_out, multiplexer_8_out,
       NewMapLevelCh, NewPlayerHP, NewPLxOM, NewPLyOM, objectONmap, p__y_2, p_x_1_y, p_x_1_y_t, p_x_2_y,
       p_x_2_y_t, p_x_y, p_x_y_1, p_x_y_1_t, p_x_y_2, playerHPCUR, PLxOM, PLyOM,
       printing_map_1_char_on_screen, subtractor_1_out, subtractor_2_out, subtractor_3_out, subtractor_4_out,
       subtractor_5_out, subtractor_6_out, subtractor_7_out, subtractor_8_out, subtractor_9_out,
       subtractor_10_out, subtractor_11_out, subtractor_12_out, subtractor_13_out, subtractor_14_out,
       weapon_1_dmg;
  wire [11:0] adder_9_out, MAP_tospace_ELEM, MapH, maps_1_p4, maps_1_p7, mapSTelemREAD, MapW, memN,
       multiplexer_4_out, p_x_1_y__elemOnMap, p_x_1_y__elemOnMap_t, p_x_2_y__elemOnMap, p_x_2_y__elemOnMap_t,
       p_x_y_1__elemOnMap, p_x_y_1__elemOnMap_t, p_x_y_2__elemOnMap, p_x_y_2__elemOnMap_t, p_x_y__elemOnMap,
       tpLen;

  Register register_1 (.D(p_x_y), .Q(INVENTORY1), .clk(INV1ch), .clr(or_1_out));  // open: en
  or or_1 (or_1_out, mainRES, itemRES1);
  Register register_2 (.D(p_x_y), .Q(INVENTORY2), .clk(INV2ch), .clr(or_2_out));  // open: en
  or or_2 (or_2_out, mainRES, itemRES2);
  Register register_3 (.D(p_x_y), .Q(INVENTORY3), .clk(INV3ch), .clr(or_3_out));  // open: en
  or or_3 (or_3_out, mainRES, itemRES3);
  Register register_4 (.D(p_x_y), .Q(INVENTORY4), .clk(INV4ch), .clr(or_4_out));  // open: en
  or or_4 (or_4_out, mainRES, itemRES4);
  Register register_5 (.D(p_x_y), .Q(INVENTORY5), .clk(INV5ch), .clr(or_5_out));  // open: en
  or or_5 (or_5_out, mainRES, itemRES5);
  Subtractor subtractor_1 (.a(InpKeyall), .b(8'h31), .out(subtractor_1_out));  // open: bin, bout
  Adder #(.width(1)) adder_1 (.a(register_6_q), .b(1'b1), .out(adder_1_out));  // open: cin, cout
  and and_1 (and_1_out, ATCinit, mainClk);
  quick quick_1 (.IN(ATCenMove), .OUT(quick_1_out));
  Random #(.width(1)) random_1 (.clk(quick_1_out), .out(random_1_out));  // open: next, clr
  quick quick_2 (.IN(ATCcorrectINP), .OUT(quick_2_out));
  and and_2 (and_2_out, _1onInp, MOVEinited, ITEMinCELL);
  quick quick_3 (.IN(and_2_out), .OUT(INV1ch));
  and and_3 (and_3_out, _2onInp, MOVEinited, ITEMinCELL);
  quick quick_4 (.IN(and_3_out), .OUT(INV2ch));
  and and_4 (and_4_out, _3onInp, MOVEinited, ITEMinCELL);
  quick quick_5 (.IN(and_4_out), .OUT(INV3ch));
  quick quick_6 (.IN(and_5_out), .OUT(INV4ch));
  and and_5 (and_5_out, _4onInp, MOVEinited, ITEMinCELL);
  quick quick_7 (.IN(and_6_out), .OUT(INV5ch));
  and and_6 (and_6_out, _5onInp, MOVEinited, ITEMinCELL);
  Multiplexer #(.select(3), .width(8), .enable("false")) multiplexer_1 (
    .in0(INVENTORY1p), .in1(INVENTORY2p), .in2(INVENTORY3p), .in3(INVENTORY4p), .in4(INVENTORY5p),
    .out(multiplexer_1_out), .sel(bit_extender_1_out));  // open: in5, in6, in7
  Bit_Extender #(.out_width(3)) bit_extender_1 (.in(subtractor_1_out), .out(bit_extender_1_out));
  Register #(.width(1)) register_6 (.D(adder_1_out), .Q(register_6_q), .clk(and_1_out), .clr(ATCnewENclc));  // open: en
  Comparator #(.width(1)) comparator_1 (.a(register_6_q), .b(1'b1), .eq(comparator_1_eq));  // open: gt, lt
  enemies enemies_1 (
    .ADDR(ATCcurEN), .ELEMIm(ENIMN), .ELEMNm(ENIMN), .Img(ENimgChrst), .Txt(ENNmChrst), .HP(enemies_1_hp),
    .DMG(ENDMGst));
  assign bit_extender_2_out = {{7{1'b0}}, random_1_out};  // Bit_Extender bit_extender_2
  Adder adder_2 (.a(bit_extender_2_out), .b(ENDMG), .out(adder_2_out));  // open: cin, cout
  quick quick_8 (.IN(quick_2_out), .OUT(quick_8_out));
  and and_7 (and_7_out, quick_8_out, ~CHHPinmove);  // AND_Gate
  and and_8 (and_8_out, and_7_out, ~ATCplWIN);  // AND_Gate
  Comparator comparator_2 (.a(INVENTORY1p), .b(8'h65), .lt(comparator_2_lt));  // open: gt, eq
  quick quick_9 (.IN(and_9_out), .OUT(itemRES1));
  and and_9 (and_9_out, comparator_2_lt, _1onInp, comparator_3_gt);
  Comparator comparator_3 (.a(INVENTORY1p), .b(8'h60), .gt(comparator_3_gt));  // open: eq, lt
  Comparator comparator_4 (.a(INVENTORY2p), .b(8'h65), .lt(comparator_4_lt));  // open: gt, eq
  quick quick_10 (.IN(and_10_out), .OUT(itemRES2));
  and and_10 (and_10_out, comparator_4_lt, _2onInp, comparator_5_gt);
  Comparator comparator_5 (.a(INVENTORY2p), .b(8'h60), .gt(comparator_5_gt));  // open: eq, lt
  Comparator comparator_6 (.a(INVENTORY3p), .b(8'h65), .lt(comparator_6_lt));  // open: gt, eq
  and and_11 (and_11_out, comparator_6_lt, _3onInp, comparator_7_gt);
  quick quick_11 (.IN(and_11_out), .OUT(itemRES3));
  Comparator comparator_7 (.a(INVENTORY3p), .b(8'h60), .gt(comparator_7_gt));  // open: eq, lt
  Comparator comparator_8 (.a(INVENTORY4p), .b(8'h65), .lt(comparator_8_lt));  // open: gt, eq
  and and_12 (and_12_out, comparator_8_lt, _4onInp, comparator_9_gt);
  quick quick_12 (.IN(and_12_out), .OUT(itemRES4));
  Comparator comparator_9 (.a(INVENTORY4p), .b(8'h60), .gt(comparator_9_gt));  // open: eq, lt
  Comparator comparator_10 (.a(INVENTORY5p), .b(8'h65), .lt(comparator_10_lt));  // open: gt, eq
  and and_13 (and_13_out, comparator_10_lt, _5onInp, comparator_11_gt);
  quick quick_13 (.IN(and_13_out), .OUT(itemRES5));
  Comparator comparator_11 (.a(INVENTORY5p), .b(8'h60), .gt(comparator_11_gt));  // open: eq, lt
  food food_1 (.FOOD(multiplexer_1_out), .GIVEHP(food_1_givehp));
  assign ATCinit = not_1_out ? not_1_out : 1'bz;  // Controlled_Buffer controlled_buffer_1
  Pull_Resistor pull_resistor_1 (.node(ATCinit));
  not not_1 (not_1_out, comparator_1_eq);
  assign ENHPst = not_1_out ? enemies_1_hp : 8'bz;  // Controlled_Buffer controlled_buffer_2
  Subtractor subtractor_2 (.a(playerHPCUR), .b(adder_2_out), .out(subtractor_2_out));  // open: bin, bout
  assign NewPlayerHP = ATCenMoved ? subtractor_2_out : 8'bz;  // Controlled_Buffer controlled_buffer_3
  assign PLAYERHPCH = ATCenMoved ? 1'b1 : 1'bz;  // Controlled_Buffer controlled_buffer_4
  Register #(.width(1)) register_7 (.D(not_2_out), .Q(ATCenMoved), .clk(and_8_out), .clr(buffer_1_out));  // open: en
  not not_2 (not_2_out, ATCenMoved);
  buf buffer_1 (buffer_1_out, PLAYERHPCH);
  Pull_Resistor pull_resistor_2 (.node(buffer_1_out));
  quick quick_14 (.IN(ATCInpFlpre), .OUT(quick_14_out));
  Comparator #(.mode("unsigned")) comparator_12 (.a(playerHPCUR), .b(8'h32), .gt(ATCplLOSE));  // open: eq, lt
  assign MAP_tospace_ELEM = mapPREst1 ? p_x_y__elemOnMap : 12'bz;  // Controlled_Buffer controlled_buffer_5
  or or_6 (mapPREst1, and_2_out, and_3_out, and_4_out, and_5_out, and_6_out);
  Adder adder_3 (.a(food_1_givehp), .b(playerHPCUR), .out(adder_3_out));  // open: cin, cout
  Pull_Resistor pull_resistor_3 (.node(pull_resistor_3_node));
  Comparator comparator_13 (.a(adder_3_out), .b(8'h32), .eq(pull_resistor_3_node));  // open: gt, lt
  quick quick_15 (.IN(quick_17_out), .OUT(quick_15_out));
  quick quick_16 (.IN(quick_15_out), .OUT(quick_16_out));
  quick quick_17 (.IN(quick_14_out), .OUT(quick_17_out));
  quick quick_18 (.IN(ATCplWIN), .OUT(quick_18_out));
  quick quick_19 (.IN(quick_20_out), .OUT(PlayerDeathRes));
  quick quick_20 (.IN(ATCplLOSE), .OUT(quick_20_out));
  quick quick_21 (.IN(mapPREst1), .OUT(stMapCLC1));
  assign InpFl1 = and_14_out ? and_14_out : 1'bz;  // Controlled_Buffer controlled_buffer_6
  and and_14 (and_14_out, mapPREst1, MOVEinited);
  Register register_8 (.D(INVENTORY1), .Q(INVENTORY1p), .clk(invchn));  // open: en, clr
  Register register_9 (.D(INVENTORY2), .Q(INVENTORY2p), .clk(invchn));  // open: en, clr
  Register register_10 (.D(INVENTORY3), .Q(INVENTORY3p), .clk(invchn));  // open: en, clr
  Register register_11 (.D(INVENTORY4), .Q(INVENTORY4p), .clk(invchn));  // open: en, clr
  Register register_12 (.D(INVENTORY5), .Q(INVENTORY5p), .clk(invchn));  // open: en, clr
  or or_7 (CHHPinmove, and_13_out, and_12_out, and_11_out, and_10_out, and_9_out);
  assign NewPlayerHP = and_15_out ? multiplexer_2_out : 8'bz;  // Controlled_Buffer controlled_buffer_7
  Multiplexer #(.width(8), .enable("false")) multiplexer_2 (
    .in0(adder_3_out), .in1(8'h32), .out(multiplexer_2_out), .sel(pull_resistor_3_node));
  assign PLAYERHPCH = and_15_out ? 1'b1 : 1'bz;  // Controlled_Buffer controlled_buffer_8
  and and_15 (and_15_out, or_8_out, CHHPinmove);
  or or_8 (or_8_out, MOVEinited, ATCInpFlpre);
  and and_16 (InpFl2, quick_16_out, ~ATCplWIN, ~ATCplLOSE);  // AND_Gate
  assign StateCh = quick_18_out ? quick_18_out : 1'bz;  // Controlled_Buffer controlled_buffer_9
  and and_17 (and_17_out, ~ITEMinCELL, or_9_out);  // AND_Gate
  and and_18 (and_18_out, and_17_out, MOVEinited);
  or or_9 (or_9_out, _1onInp, _2onInp, _3onInp, _4onInp, _5onInp);
  Comparator comparator_14 (.a(p_x_y), .b(8'h65), .lt(comparator_14_lt));  // open: gt, eq
  and and_19 (and_19_out, comparator_14_lt, comparator_15_gt);
  Comparator comparator_15 (.a(p_x_y), .b(8'h60), .gt(comparator_15_gt));  // open: eq, lt
  Comparator comparator_16 (.a(p_x_y), .b(8'h6b), .lt(comparator_16_lt));  // open: gt, eq
  and and_20 (and_20_out, comparator_16_lt, comparator_17_gt);
  Comparator comparator_17 (.a(p_x_y), .b(8'h65), .gt(comparator_17_gt));  // open: eq, lt
  assign InpFl1 = and_18_out ? and_18_out : 1'bz;  // Controlled_Buffer controlled_buffer_10
  or or_10 (ITEMinCELL, and_19_out, and_20_out);
  Adder #(.width(4)) adder_4 (.a(register_13_q), .b(4'b0001), .out(adder_4_out));  // open: cin, cout
  Comparator #(.width(2)) comparator_18 (.a(PlDir), .b(2'b00), .eq(comparator_18_eq));  // open: gt, lt
  Comparator #(.width(2)) comparator_19 (.a(PlDir), .b(2'b10), .eq(comparator_19_eq));  // open: gt, lt
  Comparator #(.width(2)) comparator_20 (.a(PlDir), .b(2'b01), .eq(comparator_20_eq));  // open: gt, lt
  Comparator #(.width(2)) comparator_21 (.a(PlDir), .b(2'b11), .eq(comparator_21_eq));  // open: gt, lt
  Comparator #(.width(4)) comparator_22 (
    .a(4'b1100), .b(register_13_q), .gt(comparator_22_gt), .eq(comparator_22_eq), .lt(comparator_22_lt));
  Register #(.width(4)) register_13 (
    .D(adder_4_out), .Q(register_13_q), .clk(and_21_out), .clr(InpFlpreC));  // open: en
  and and_21 (and_21_out, or_13_out, mainClk);
  Comparator #(.width(4)) comparator_23 (.a(register_13_q), .b(4'b0010), .eq(comparator_23_eq));  // open: gt, lt
  Comparator #(.width(4)) comparator_24 (.a(register_13_q), .b(4'b0011), .eq(comparator_24_eq));  // open: gt, lt
  Comparator #(.width(4)) comparator_25 (.a(register_13_q), .b(4'b0011), .eq(comparator_25_eq));  // open: gt, lt
  Comparator #(.width(4)) comparator_26 (.a(register_13_q), .b(4'b0100), .eq(comparator_26_eq));  // open: gt, lt
  Comparator #(.width(4)) comparator_27 (.a(register_13_q), .b(4'b0100), .eq(comparator_27_eq));  // open: gt, lt
  Comparator #(.width(4)) comparator_28 (.a(register_13_q), .b(4'b0101), .eq(comparator_28_eq));  // open: gt, lt
  Comparator #(.width(4)) comparator_29 (.a(register_13_q), .b(4'b0101), .eq(comparator_29_eq));  // open: gt, lt
  Comparator #(.width(4)) comparator_30 (.a(register_13_q), .b(4'b0110), .eq(comparator_30_eq));  // open: gt, lt
  Comparator #(.width(4)) comparator_31 (.a(register_13_q), .b(4'b0110), .eq(comparator_31_eq));  // open: gt, lt
  Comparator #(.width(4)) comparator_32 (.a(register_13_q), .b(4'b0111), .eq(comparator_32_eq));  // open: gt, lt
  Comparator #(.width(4)) comparator_33 (.a(register_13_q), .b(4'b0111), .eq(comparator_33_eq));  // open: gt, lt
  Comparator #(.width(4)) comparator_34 (.a(register_13_q), .b(4'b1000), .eq(comparator_34_eq));  // open: gt, lt
  Comparator #(.width(4)) comparator_35 (.a(register_13_q), .b(4'b1000), .eq(comparator_35_eq));  // open: gt, lt
  Comparator #(.width(4)) comparator_36 (.a(register_13_q), .b(4'b1001), .eq(comparator_36_eq));  // open: gt, lt
  Comparator #(.width(4)) comparator_37 (.a(register_13_q), .b(4'b1001), .eq(comparator_37_eq));  // open: gt, lt
  Comparator #(.width(4)) comparator_38 (.a(register_13_q), .b(4'b1010), .eq(comparator_38_eq));  // open: gt, lt
  Comparator #(.width(4)) comparator_39 (.a(register_13_q), .b(4'b1010), .eq(comparator_39_eq));  // open: gt, lt
  Comparator #(.width(4)) comparator_40 (.a(register_13_q), .b(4'b1011), .eq(comparator_40_eq));  // open: gt, lt
  not not_3 (not_3_out, comparator_41_eq);
  Comparator comparator_41 (.a(p_x_y_1_t), .b(8'h23), .eq(comparator_41_eq));  // open: gt, lt
  Comparator comparator_42 (.a(p_x_y_1), .b(8'h23), .eq(comparator_42_eq));  // open: gt, lt
  not not_4 (not_4_out, comparator_42_eq);
  not not_5 (not_5_out, comparator_43_eq);
  Comparator comparator_43 (.a(p_x_1_y), .b(8'h23), .eq(comparator_43_eq));  // open: gt, lt
  not not_6 (not_6_out, comparator_44_eq);
  Comparator comparator_44 (.a(p_x_1_y_t), .b(8'h23), .eq(comparator_44_eq));  // open: gt, lt
  Register register_14 (.D(NewMapLevelCh), .Q(mapLevelCur), .clk(MapLevelCh), .clr(mainRES));  // open: en
  Register register_15 (.D(NewPlayerHP), .Q(playerHPCUR), .clk(pull_resistor_4_node), .clr(mainRES));  // open: en
  Pull_Resistor pull_resistor_4 (.node(pull_resistor_4_node));
  buf buffer_2 (pull_resistor_4_node, PLAYERHPCH);
  Register #(.width(2)) register_16 (.D(ATCnewEN), .Q(ATCcurEN), .clk(ATCnewENclc));  // open: en, clr
  Register register_17 (.D(ENHP), .Q(LENHP), .clk(or_11_out));  // open: en, clr
  or or_11 (or_11_out, quick_22_out, quick_23_out);
  quick quick_22 (.IN(ATCinisW), .OUT(quick_22_out));
  quick quick_23 (.IN(ATCinit), .OUT(quick_23_out));
  quick quick_24 (.IN(demultiplexer_1_out1), .OUT(InpFlpreC));
  Demultiplexer #(.select(2), .disabled(0), .enable("false")) demultiplexer_1 (
    .out0(InpFlpreSTRT), .out1(demultiplexer_1_out1), .out2(ATCInpFlpre), .in(invchn), .sel(gameState));  // open: out3
  or or_12 (letsPrint, memReadyToPrint, gS0);
  or or_13 (or_13_out, comparator_22_gt, comparator_22_lt);
  Subtractor subtractor_3 (.a(PLyOM), .b(8'h1), .out(subtractor_3_out));  // open: bin, bout
  and and_22 (and_22_out, not_3_out, WonInp, comparator_18_eq);
  Adder adder_5 (.a(PLyOM), .b(8'h1), .out(adder_5_out));  // open: cin, cout
  and and_23 (and_23_out, not_4_out, WonInp, comparator_19_eq);
  Adder adder_6 (.a(PLxOM), .b(8'h1), .out(adder_6_out));  // open: cin, cout
  and and_24 (and_24_out, not_5_out, WonInp, comparator_20_eq);
  Subtractor subtractor_4 (.a(PLxOM), .b(8'h1), .out(subtractor_4_out));  // open: bin, bout
  and and_25 (and_25_out, not_6_out, WonInp, comparator_21_eq);
  Comparator comparator_45 (.a(INVENTORY1p), .b(8'h6b), .lt(comparator_45_lt));  // open: gt, eq
  and and_26 (and_26_out, comparator_45_lt, _1onInp, comparator_46_gt);
  Comparator comparator_46 (.a(INVENTORY1p), .b(8'h65), .gt(comparator_46_gt));  // open: eq, lt
  Comparator comparator_47 (.a(INVENTORY2p), .b(8'h6b), .lt(comparator_47_lt));  // open: gt, eq
  and and_27 (and_27_out, comparator_47_lt, _2onInp, comparator_48_gt);
  Comparator comparator_48 (.a(INVENTORY2p), .b(8'h65), .gt(comparator_48_gt));  // open: eq, lt
  Comparator comparator_49 (.a(INVENTORY3p), .b(8'h6b), .lt(comparator_49_lt));  // open: gt, eq
  and and_28 (and_28_out, comparator_49_lt, _3onInp, comparator_50_gt);
  Comparator comparator_50 (.a(INVENTORY3p), .b(8'h65), .gt(comparator_50_gt));  // open: eq, lt
  Comparator comparator_51 (.a(INVENTORY4p), .b(8'h6b), .lt(comparator_51_lt));  // open: gt, eq
  and and_29 (and_29_out, comparator_51_lt, _4onInp, comparator_52_gt);
  Comparator comparator_52 (.a(INVENTORY4p), .b(8'h65), .gt(comparator_52_gt));  // open: eq, lt
  Comparator comparator_53 (.a(INVENTORY5p), .b(8'h6b), .lt(comparator_53_lt));  // open: gt, eq
  and and_30 (and_30_out, comparator_53_lt, _5onInp, comparator_54_gt);
  Comparator comparator_54 (.a(INVENTORY5p), .b(8'h65), .gt(comparator_54_gt));  // open: eq, lt
  consoler CONSOLE_PRINTER (
    .CLK(mainClk), .RESET(letsPrint), .IT_WORKED(invchn), .INPUT_CHAR(InpKeyall), .PRINT_SIZE(tpLen),
    .MEM_A(memN), .MEM_D(memChar), .CONNECTED(CONSOLE_PRINTER_connected));  // open: INPUT_were
  Lquick lquick_1 (.IN(comparator_22_eq), .OUT(MOVEinited), .CLC(mainClk));
  assign MAP_tospace_ELEM = comparator_23_eq ? p_x_y__elemOnMap : 12'bz;  // Controlled_Buffer controlled_buffer_11
  assign MAP_tospace_ELEM = comparator_25_eq ? p_x_y_1__elemOnMap_t : 12'bz;  // Controlled_Buffer controlled_buffer_12
  assign MAP_tospace_ELEM = comparator_27_eq ? p_x_y_1__elemOnMap : 12'bz;  // Controlled_Buffer controlled_buffer_13
  assign MAP_tospace_ELEM = comparator_29_eq ? p_x_1_y__elemOnMap_t : 12'bz;  // Controlled_Buffer controlled_buffer_14
  assign MAP_tospace_ELEM = comparator_31_eq ? p_x_1_y__elemOnMap : 12'bz;  // Controlled_Buffer controlled_buffer_15
  assign MAP_tospace_ELEM = comparator_33_eq ? p_x_2_y__elemOnMap : 12'bz;  // Controlled_Buffer controlled_buffer_16
  assign MAP_tospace_ELEM = comparator_35_eq ? p_x_2_y__elemOnMap_t : 12'bz;  // Controlled_Buffer controlled_buffer_17
  assign MAP_tospace_ELEM = comparator_37_eq ? p_x_y_2__elemOnMap_t : 12'bz;  // Controlled_Buffer controlled_buffer_18
  assign MAP_tospace_ELEM = comparator_39_eq ? p_x_y_2__elemOnMap : 12'bz;  // Controlled_Buffer controlled_buffer_19
  assign NewPLyOM = and_22_out ? subtractor_3_out : 8'bz;  // Controlled_Buffer controlled_buffer_20
  assign NewPLyOM = and_23_out ? adder_5_out : 8'bz;  // Controlled_Buffer controlled_buffer_21
  assign NewPLxOM = and_24_out ? adder_6_out : 8'bz;  // Controlled_Buffer controlled_buffer_22
  assign NewPLxOM = and_25_out ? subtractor_4_out : 8'bz;  // Controlled_Buffer controlled_buffer_23
  assign InpFl1 = and_31_out ? and_31_out : 1'bz;  // Controlled_Buffer controlled_buffer_24
  and and_31 (and_31_out, MOVEinited, WonInp);
  and and_32 (ATCinisW, ATCInpFlpre, or_14_out);
  or or_14 (or_14_out, and_26_out, and_27_out, and_28_out, and_29_out, and_30_out);
  buf buffer_3 (buffer_3_out, StateCh);
  Pull_Resistor pull_resistor_5 (.node(buffer_3_out));
  Register register_18 (.D(ENDMGst), .Q(ENDMG), .clk(ATCinit));  // open: en, clr
  Register register_19 (.D(ENHPst), .Q(ENHP), .clk(or_15_out));  // open: en, clr
  or or_15 (or_15_out, ATCnEhp, ATCinit);
  Demultiplexer #(.select(2), .width(8), .disabled(0), .enable("false")) demultiplexer_2 (
    .out1(InpKey), .out2(ATCInpKey), .in(InpKeyall), .sel(gameState));  // open: out0, out3
  LED connected (.in(CONSOLE_PRINTER_connected));
  LED data_was ();  // open: in
  Register register_20 (.D(objectONmap), .Q(p_x_y), .clk(comparator_24_eq));  // open: en, clr
  Register register_21 (.D(objectONmap), .Q(p_x_y_1_t), .clk(comparator_26_eq));  // open: en, clr
  Register register_22 (.D(objectONmap), .Q(p_x_y_1), .clk(comparator_28_eq));  // open: en, clr
  Register register_23 (.D(objectONmap), .Q(p_x_1_y_t), .clk(comparator_30_eq));  // open: en, clr
  Register register_24 (.D(objectONmap), .Q(p_x_1_y), .clk(comparator_32_eq));  // open: en, clr
  Register register_25 (.D(objectONmap), .Q(p_x_2_y), .clk(comparator_34_eq));  // open: en, clr
  Register register_26 (.D(objectONmap), .Q(p_x_2_y_t), .clk(comparator_36_eq));  // open: en, clr
  Register register_27 (.D(objectONmap), .Q(p_x_y_2), .clk(comparator_38_eq));  // open: en, clr
  Register register_28 (.D(objectONmap), .Q(p__y_2), .clk(comparator_40_eq));  // open: en, clr
  or or_16 (or_16_out, and_22_out, and_23_out);
  or or_17 (or_17_out, and_24_out, and_25_out);
  Register #(.width(2)) register_29 (.D(gSto), .Q(gameState), .clk(buffer_3_out), .clr(mainRES));  // open: en
  Register #(.width(2)) register_30 (.D(NewPlDir), .Q(PlDir), .clk(PlDirCh), .clr(mainRES));  // open: en
  quick quick_25 (.IN(or_16_out), .OUT(changePCy));
  quick quick_26 (.IN(or_17_out), .OUT(changePCx));
  Subtractor subtractor_5 (.a(ATCInpKey), .b(8'h31), .out(subtractor_5_out));  // open: bin, bout
  x_y__to_memory_elem_number x_y_____elem (.H(MapW), .Y(PLyOM), .X(PLxOM), .ELEM(p_x_y__elemOnMap), .START(12'h4));
  x_y__to_memory_elem_number x_y_____elem_2 (
    .H(MapW), .Y(adder_7_out), .X(PLxOM), .ELEM(p_x_y_1__elemOnMap), .START(12'h4));
  Adder adder_7 (.a(PLyOM), .b(8'h1), .out(adder_7_out));  // open: cin, cout
  x_y__to_memory_elem_number x_y_____elem_3 (
    .H(MapW), .Y(PLyOM), .X(adder_8_out), .ELEM(p_x_1_y__elemOnMap), .START(12'h4));
  Adder adder_8 (.a(PLxOM), .b(8'h1), .out(adder_8_out));  // open: cin, cout
  Comparator comparator_55 (.a(InpKeyall), .b(8'h31), .eq(_1onInp));  // open: gt, lt
  Comparator comparator_56 (.a(InpKeyall), .b(8'h32), .eq(_2onInp));  // open: gt, lt
  Comparator comparator_57 (.a(InpKeyall), .b(8'h33), .eq(_3onInp));  // open: gt, lt
  Comparator comparator_58 (.a(InpKeyall), .b(8'h34), .eq(_4onInp));  // open: gt, lt
  Comparator comparator_59 (.a(InpKeyall), .b(8'h35), .eq(_5onInp));  // open: gt, lt
  Comparator comparator_60 (.a(InpKey), .b(8'h61), .eq(AonInp));  // open: gt, lt
  Comparator comparator_61 (.a(InpKey), .b(8'h64), .eq(DonInp));  // open: gt, lt
  Comparator comparator_62 (.a(InpKey), .b(8'h77), .eq(WonInp));  // open: gt, lt
  quick quick_27 (.IN(comparator_63_eq), .OUT(qres));
  Comparator comparator_63 (.a(InpKey), .b(8'h71), .eq(comparator_63_eq));  // open: gt, lt
  Comparator #(.width(2)) comparator_64 (.a(PlDir), .b(2'b00), .eq(comparator_64_eq));  // open: gt, lt
  Comparator #(.width(2)) comparator_65 (.a(PlDir), .b(2'b10), .eq(comparator_65_eq));  // open: gt, lt
  Comparator #(.width(2)) comparator_66 (.a(PlDir), .b(2'b01), .eq(comparator_66_eq));  // open: gt, lt
  Comparator #(.width(2)) comparator_67 (.a(PlDir), .b(2'b11), .eq(comparator_67_eq));  // open: gt, lt
  Multiplexer #(.select(3), .width(8), .enable("false")) multiplexer_3 (
    .in0(INVENTORY1p), .in1(INVENTORY2p), .in2(INVENTORY3p), .in3(INVENTORY4p), .in4(INVENTORY5p),
    .out(multiplexer_3_out), .sel(bit_extender_3_out));  // open: in5, in6, in7
  Bit_Extender #(.out_width(3)) bit_extender_3 (.in(subtractor_5_out), .out(bit_extender_3_out));
  Multiplexer #(.width(12), .enable("false")) multiplexer_4 (
    .in0(MAP_tospace_ELEM), .in1(mapSTelemREAD), .out(multiplexer_4_out), .sel(not_7_out));
  Register #(.width(12)) register_31 (.D(adder_9_out), .Q(mapSTelemREAD), .clk(and_33_out), .clr(mainRES));  // open: en
  Adder #(.width(12)) adder_9 (.a(mapSTelemREAD), .b(12'h1), .out(adder_9_out));  // open: cin, cout
  and and_33 (and_33_out, not_7_out, mainClk);
  // Probe on memN
  // Probe on memN
  Button button_1 (.out(button_1_out));
  and and_34 (and_34_out, WalkProcessed, gS1);
  xor xor_1 (xor_1_out, and_34_out, and_35_out);
  and and_35 (and_35_out, InpFl2, gS2);
  Comparator comparator_68 (.a(p_x_y_1_t), .b(8'h30), .gt(comparator_68_gt));  // open: eq, lt
  Comparator comparator_69 (.a(p_x_y_1), .b(8'h30), .gt(comparator_69_gt));  // open: eq, lt
  Comparator comparator_70 (.a(p_x_1_y), .b(8'h30), .gt(comparator_70_gt));  // open: eq, lt
  Comparator comparator_71 (.a(p_x_1_y_t), .b(8'h30), .gt(comparator_71_gt));  // open: eq, lt
  quick quick_28 (.IN(ATCinisW), .OUT(quick_28_out));
  Pull_Resistor pull_resistor_6 (.node(pull_resistor_6_node));
  weapon weapon_1 (.WEAPON(multiplexer_3_out), .DMG(weapon_1_dmg), .GenRnd(quick_28_out));
  Comparator #(.mode("unsigned")) comparator_72 (
    .a(weapon_1_dmg), .b(LENHP), .gt(pull_resistor_6_node), .eq(comparator_72_eq), .lt(comparator_72_lt));
  LED led_1 (.in(memReadyToPrint));
  or or_18 (memReadyToPrint, button_1_out, quick_29_out);
  quick quick_29 (.IN(xor_1_out), .OUT(quick_29_out));
  Subtractor subtractor_6 (.a(PLyOM), .b(8'h1), .out(subtractor_6_out));  // open: bin, bout
  Subtractor subtractor_7 (.a(PLxOM), .b(8'h1), .out(subtractor_7_out));  // open: bin, bout
  Adder adder_10 (.a(PLxOM), .b(8'h2), .out(adder_10_out));  // open: cin, cout
  Comparator comparator_73 (.a(p_x_y_1_t), .b(8'h35), .lt(comparator_73_lt));  // open: gt, eq
  Comparator comparator_74 (.a(p_x_y_1), .b(8'h35), .lt(comparator_74_lt));  // open: gt, eq
  Comparator comparator_75 (.a(p_x_1_y), .b(8'h35), .lt(comparator_75_lt));  // open: gt, eq
  Comparator comparator_76 (.a(p_x_1_y_t), .b(8'h35), .lt(comparator_76_lt));  // open: gt, eq
  or or_19 (ATCcorrectINP, _1onInp, _2onInp, _3onInp, _4onInp, _5onInp);
  or or_20 (or_20_out, pull_resistor_6_node, comparator_72_eq);
  Pull_Resistor pull_resistor_7 (.node(comparator_72_eq));
  Pull_Resistor pull_resistor_8 (.node(comparator_72_lt));
  Multiplexer #(.width(8), .enable("false")) multiplexer_5 (
    .in0(8'h20), .in1(mapSTDATAreaded), .out(multiplexer_5_out), .sel(not_7_out));
  not not_7 (not_7_out, comparator_77_eq);
  Comparator #(.width(12)) comparator_77 (.a(mapSTelemREAD), .b(12'h94), .eq(comparator_77_eq));  // open: gt, lt
  printing_map printing_map_1 (
    .Xpp(PLxOM), .Ypp(PLyOM), .Clock(mainClk), .Num_of_elem(gStdtScrMem), .Mem_N(memN),
    .Char_on_screen(printing_map_1_char_on_screen), .Cond_of_change(printing_map_1_cond_of_change),
    .No_of_map(mapLevelCur), .Main_Res(memReadyToPrint), .Direction(PlDir));
  x_y__to_memory_elem_number x_y_____elem_4 (
    .H(MapW), .Y(subtractor_6_out), .X(PLxOM), .ELEM(p_x_y_1__elemOnMap_t), .START(12'h4));
  x_y__to_memory_elem_number x_y_____elem_5 (
    .H(MapW), .Y(PLyOM), .X(subtractor_7_out), .ELEM(p_x_1_y__elemOnMap_t), .START(12'h4));
  x_y__to_memory_elem_number x_y_____elem_6 (
    .H(MapW), .Y(PLyOM), .X(adder_10_out), .ELEM(p_x_2_y__elemOnMap), .START(12'h4));
  Subtractor subtractor_8 (.a(p_x_y_1_t), .b(8'h31), .out(subtractor_8_out));  // open: bin, bout
  Subtractor subtractor_9 (.a(p_x_1_y_t), .b(8'h31), .out(subtractor_9_out));  // open: bin, bout
  and and_36 (ATCplWIN, ATCcorrectINP, and_37_out);
  and and_37 (and_37_out, or_20_out, ATCinisW);
  and and_38 (ATCplAttaked, ATCinisW, comparator_72_lt);
  quick quick_30 (.IN(ATCplAttaked), .OUT(ATCnEhp));
  assign ENHPst = ATCplAttaked ? subtractor_10_out : 8'bz;  // Controlled_Buffer controlled_buffer_25
  Subtractor subtractor_10 (.a(ENHP), .b(weapon_1_dmg), .out(subtractor_10_out));  // open: bin, bout
  or or_21 (stMapCLC, and_33_out, stMapCLC1, stMapCLC2);
  graphic_elems graphic_elems_1 (.ADDR(gStdtScrMem), .ELEM(memN), .DATA(graphic_elems_1_data), .LEN(tpLen));
  assign MAP_tospace_ELEM = and_39_out ? p_x_y_1__elemOnMap_t : 12'bz;  // Controlled_Buffer controlled_buffer_26
  assign ATCnewEN = and_39_out ? bit_extender_4_out : 2'bz;  // Controlled_Buffer controlled_buffer_27
  Bit_Extender #(.out_width(2)) bit_extender_4 (.in(subtractor_8_out), .out(bit_extender_4_out));
  and and_39 (and_39_out, comparator_68_gt, comparator_73_lt, comparator_64_eq);
  and and_40 (and_40_out, comparator_69_gt, comparator_74_lt, comparator_65_eq);
  and and_41 (and_41_out, comparator_70_gt, comparator_75_lt, comparator_66_eq);
  and and_42 (and_42_out, comparator_71_gt, comparator_76_lt, comparator_67_eq);
  assign ATCnewEN = and_42_out ? bit_extender_5_out : 2'bz;  // Controlled_Buffer controlled_buffer_28
  Bit_Extender #(.out_width(2)) bit_extender_5 (.in(subtractor_9_out), .out(bit_extender_5_out));
  assign MAP_tospace_ELEM = and_42_out ? p_x_1_y__elemOnMap_t : 12'bz;  // Controlled_Buffer controlled_buffer_29
  RAM #(.addrWidth(12), .bus("separate")) ram_1 (
    .addr(multiplexer_4_out), .din(multiplexer_5_out), .data(objectONmap), .str(mapPREst), .clk(stMapCLC));  // open: sel, ld, clr
  or or_22 (mapPREst, not_7_out, ATCnewENclc, mapPREst1);
  assign memChar = not_8_out ? graphic_elems_1_data : 8'bz;  // Controlled_Buffer controlled_buffer_30
  not not_8 (not_8_out, printing_map_1_cond_of_change);
  // Probe on memChar
  assign memChar = printing_map_1_cond_of_change ? printing_map_1_char_on_screen : 8'bz;  // Controlled_Buffer controlled_buffer_31
  not not_9 (not_9_out, or_23_out);
  or or_23 (or_23_out, AonInp, DonInp);
  Subtractor subtractor_11 (.a(p_x_y_1), .b(8'h31), .out(subtractor_11_out));  // open: bin, bout
  and and_43 (ATCnewENclc, MOVEinited, buffer_4_out);
  or or_24 (MOVEenHERE, and_39_out, and_40_out, and_41_out, and_42_out);
  buf buffer_4 (buffer_4_out, MOVEenHERE);
  Subtractor subtractor_12 (.a(p_x_1_y), .b(8'h31), .out(subtractor_12_out));  // open: bin, bout
  x_y__to_memory_elem_number x_y_____elem_7 (
    .H(MapW), .Y(subtractor_13_out), .X(PLxOM), .ELEM(p_x_y_2__elemOnMap_t), .START(12'h4));
  Subtractor subtractor_13 (.a(PLyOM), .b(8'h2), .out(subtractor_13_out));  // open: bin, bout
  x_y__to_memory_elem_number x_y_____elem_8 (
    .H(MapW), .Y(PLyOM), .X(subtractor_14_out), .ELEM(p_x_2_y__elemOnMap_t), .START(12'h4));
  Subtractor subtractor_14 (.a(PLxOM), .b(8'h2), .out(subtractor_14_out));  // open: bin, bout
  x_y__to_memory_elem_number x_y_____elem_9 (
    .H(MapW), .Y(adder_11_out), .X(PLyOM), .ELEM(p_x_y_2__elemOnMap), .START(12'h4));
  Adder adder_11 (.a(PLxOM), .b(8'h2), .out(adder_11_out));  // open: cin, cout
  Adder #(.width(2)) adder_12 (.a(PlDir), .b(2'b01), .out(adder_12_out));  // open: cin, cout
  Subtractor #(.width(2)) subtractor_15 (.a(PlDir), .b(2'b01), .out(subtractor_15_out));  // open: bin, bout
  and and_44 (and_44_out, MOVEinited, not_10_out);
  not not_10 (not_10_out, not_9_out);
  quick quick_31 (.IN(not_10_out), .OUT(PlDirCh));
  assign InpFl1 = and_45_out ? and_45_out : 1'bz;  // Controlled_Buffer controlled_buffer_32
  and and_45 (and_45_out, MOVEinited, ~or_25_out);  // AND_Gate
  or or_25 (or_25_out, _1onInp, _2onInp, _3onInp, _4onInp, _5onInp, AonInp, DonInp, WonInp);
  assign MAP_tospace_ELEM = and_40_out ? p_x_y_1__elemOnMap : 12'bz;  // Controlled_Buffer controlled_buffer_33
  assign ATCnewEN = and_40_out ? bit_extender_6_out : 2'bz;  // Controlled_Buffer controlled_buffer_34
  Bit_Extender #(.out_width(2)) bit_extender_6 (.in(subtractor_11_out), .out(bit_extender_6_out));
  not not_11 (not_11_out, not_12_out);
  not not_12 (not_12_out, not_13_out);
  not not_13 (not_13_out, ATCnewENclc);
  assign StateCh = ATCnewENclc ? ATCnewENclc : 1'bz;  // Controlled_Buffer controlled_buffer_35
  Bit_Extender #(.out_width(2)) bit_extender_7 (.in(subtractor_12_out), .out(bit_extender_7_out));
  assign ATCnewEN = and_41_out ? bit_extender_7_out : 2'bz;  // Controlled_Buffer controlled_buffer_36
  assign MAP_tospace_ELEM = and_41_out ? p_x_1_y__elemOnMap : 12'bz;  // Controlled_Buffer controlled_buffer_37
  Multiplexer #(.width(2), .enable("false")) multiplexer_6 (
    .in0(adder_12_out), .in1(subtractor_15_out), .out(NewPlDir), .sel(AonInp));
  assign InpFl1 = and_44_out ? and_44_out : 1'bz;  // Controlled_Buffer controlled_buffer_38
  not not_14 (stMapCLC2, not_11_out);
  not not_15 (not_15_out, pull_resistor_9_node);
  Pull_Resistor pull_resistor_9 (.node(pull_resistor_9_node));
  not not_16 (not_16_out, not_15_out);
  buf buffer_5 (pull_resistor_9_node, InpFl1);
  LED led_2 (.in(demultiplexer_3_out3));
  LED led_3 (.in(demultiplexer_3_out3));
  and and_46 (WalkProcessed, ~MOVEenHERE, not_16_out);  // AND_Gate
  Multiplexer #(.width(8), .enable("false")) multiplexer_7 (
    .in0(NewPLxOM), .in1(maps_1_p3), .out(multiplexer_7_out), .sel(gS0));
  or or_26 (or_26_out, changePCx, LoadMap);
  Register #(.width(12)) u_mapW (.D(maps_1_p4), .Q(MapW), .clk(LoadMap), .clr(mainRES));  // open: en
  Button button_2 (.out(button_2_out));
  LED led_4 (.in(demultiplexer_3_out0));
  LED led_5 (.in(demultiplexer_3_out0));
  LED led_6 (.in(demultiplexer_3_out1));
  Demultiplexer #(.select(2), .enable("false")) demultiplexer_3 (
    .out0(demultiplexer_3_out0), .out1(demultiplexer_3_out1), .out2(demultiplexer_3_out2),
    .out3(demultiplexer_3_out3), .in(1'b1), .sel(PlDir));
  LED led_7 (.in(demultiplexer_3_out1));
  LED led_8 (.in(demultiplexer_3_out2));
  LED led_9 (.in(demultiplexer_3_out2));
  LED led_10 (.in(demultiplexer_4_out0));
  LED led_11 (.in(demultiplexer_4_out1));
  LED led_12 (.in(demultiplexer_4_out2));
  Register Xpp (.D(multiplexer_7_out), .Q(PLxOM), .clk(or_26_out));  // open: en, clr
  Comparator #(.width(2)) comparator_78 (.a(2'b00), .b(gameState), .eq(gS0));  // open: gt, lt
  Comparator #(.width(2)) comparator_79 (.a(2'b01), .b(gameState), .eq(gS1));  // open: gt, lt
  Comparator #(.width(2)) comparator_80 (.a(2'b10), .b(gameState), .eq(gS2));  // open: gt, lt
  and and_47 (mainClk, ~mainRES, clock_1_out);  // AND_Gate
  Clock clock_1 (.out(clock_1_out));
  or or_27 (mainRES, PlayerDeathRes, button_2_out, qres);
  // Probe on playerHPCUR
  // Probe on ENHP
  // Probe on ATCcurEN
  Demultiplexer #(.select(2), .enable("false")) demultiplexer_4 (
    .out0(demultiplexer_4_out0), .out1(demultiplexer_4_out1), .out2(demultiplexer_4_out2), .in(1'b1),
    .sel(gameState));  // open: out3
  Register #(.width(12)) u_mapH (.D(maps_1_p7), .Q(MapH), .clk(LoadMap), .clr(mainRES));  // open: en
  assign NewPlayerHP = LoadMap ? 8'ha : 8'bz;  // Controlled_Buffer controlled_buffer_39
  buf buffer_6 (LoadMap, and_48_out);
  and and_48 (and_48_out, InpFlpreSTRT, gS0);
  quick quick_32 (.IN(chGM), .OUT(quick_32_out));
  // Probe on PLxOM
  // Probe on PLyOM
  Register Ypp (.D(multiplexer_8_out), .Q(PLyOM), .clk(or_28_out));  // open: en, clr
  Multiplexer #(.width(8), .enable("false")) multiplexer_8 (
    .in0(NewPLyOM), .in1(maps_1_p5), .out(multiplexer_8_out), .sel(gS0));
  or or_28 (or_28_out, changePCy, LoadMap);
  // maps maps_1: pin names not known; wires that end beside it: mapLevelCur, mapSTelemREAD, maps_1_p3, maps_1_p4, maps_1_p5, maps_1_p4, maps_1_p7, mapSTDATAreaded
  or or_29 (or_29_out, and_48_out, quick_32_out);
  assign StateCh = or_29_out ? or_29_out : 1'bz;  // Controlled_Buffer controlled_buffer_40
  assign PLAYERHPCH = quick_33_out ? quick_33_out : 1'bz;  // Controlled_Buffer controlled_buffer_41
  quick quick_33 (.IN(or_29_out), .OUT(quick_33_out));
  Multiplexer #(.select(2), .width(2), .enable("false")) multiplexer_9 (
    .in0(2'b01), .in1(2'b10), .in2(2'b01), .out(gSto), .sel({gS2, gS1}));  // open: in3
  Multiplexer #(.select(2), .width(8), .enable("false")) multiplexer_10 (
    .in0(8'h1f), .in1({8{1'b0}}), .in2(8'h1e), .out(gStdtScrMem), .sel({gS2, gS1}));  // open: in3

  // Other names for the same wires on the sheet: ATCinit1 = ATCinit; mapPREst2 = ATCnewENclc;
  //   p_x_y_obj[7:0] = objectONmap

  // Notes on the sheet:
  //   INVETORY
  //   BATTLE MODE
  //   CURRENT STATE
  //   REMOVE ITEM FROM GAME MAP
  //   For work enemy win
  //   is it eat in cell
  //   is it weapon in cell
  //   PREVIOUS STATE
  //   EAT FOOD
  //   ENEMY INIT
  //   ENEMY ATTACK
  //   enemy attaked
  //   If PLAYER WON
  //   CHECK ENEMY WON
  //   INVENTORY REGISTERS
  //   GET ITEM
  //   PLAYER MOVEMENT
  //   SOME GLOBAL VARIBLES
  //   Curent map level
  //   Player HP
  //   Current Enemy number
  //   Last Enemy hp
  //   BATTLE MODE VARIBLES
  //   PRINTING ON SCREEN
  //   GET SOME ADJACENT CELLS
  //   weapon in cell
  //   Game state
  //   0 - start screen 1 - walking 2 - battle
  //   Player Direction
  //   Current Enemy dmg
  //   Current Enemy hp
  //   DO FORWARD STEP
  //   0
  //   3
  //   ->
  //   1
  //   2
  //   Player (y+1,x) cell
  //   Player (y,x+1) cell
  //   GAME MAP
  //   RENDERING OF SCREEN
  //   Player cell
  //   inp: 1
  //   inp: 2
  //   inp: 3
  //   inp: 4
  //   inp: 5
  //   inp: a
  //   inp: d
  //   inp: w
  //   inp: q
  //   Player (y-1,x) cell
  //   Player (y,x-1) cell
  //   Player (y,x+2) cell
  //   RENDERING COMPLITE
  //   player won
  //   GET SOME ADJACENT CELLS COORDINATES
  //   Player (y-2,x) cell
  //   Player (y,x-2) cell
  //   Player (y+2,x) cell
  //   MEET ENEMY AND CHANGE GAME MODE TO BATTLE
  //   ATTACK THE ENEMY
  //   FOR WORK.....
  //   Memory access
  //   PARSE INPUT
  //   MAKE A TURN
  //   turn were
  //   uncorrect input
  //   START
  //   WALK
  //   BATTLE
  //   reset game
  //   pHP
  //   eHP
  //   curENEMY
  //   INITIALIZING GAME MAP
  //   GAME MODE CHANGER
  //   DEBUG TOOLS
  //   GAME INFORAMTION
  //   player direction
  //   pX
  //   pY
endmodule

// CP
module consoler (
  input  [7:0] MEM_D,
  input  CLK,
  input  [11:0] PRINT_SIZE,
  input  RESET,
  output IT_WORKED,
  output [7:0] INPUT_CHAR,
  output CONNECTED,
  output INPUT_were,
  output [11:0] MEM_A
);

  wire and_3_out, and_4_out, clc, comparator_1_eq, not_1_out, not_2_out, not_3_out, not_4_out, not_5_out,
       not_6_out, or_1_out, PRND, readConsole, register_2_q, RES, RESET_MEMORY_COUNTER_out, uart_1_p3,
       uart_1_p7;
  wire [7:0] uart_1_p1;
  wire [11:0] adder_1_out;

  and and_1 (IT_WORKED, not_3_out, PRND, INPUT_were);
  Register #(.width(1)) register_1 (.D(not_1_out), .Q(INPUT_were), .clk(or_1_out));  // open: en, clr
  not not_1 (not_1_out, INPUT_were);
  or or_1 (or_1_out, RES, uart_1_p3);
  and and_2 (clc, CLK, not_2_out);
  not not_2 (not_2_out, RES);
  not not_3 (not_3_out, uart_1_p3);
  not not_4 (not_4_out, RESET);
  and and_3 (and_3_out, clc, comparator_1_eq);
  Register #(.width(1)) register_2 (.D(RESET), .Q(register_2_q), .clk(RESET), .clr(not_5_out));  // open: en
  not not_5 (not_5_out, not_4_out);
  Register register_3 (.D(uart_1_p1), .Q(INPUT_CHAR), .clk(and_3_out), .clr(RES));  // open: en
  or or_2 (RES, register_2_q, RESET_MEMORY_COUNTER_out);
  Button RESET_MEMORY_COUNTER (.out(RESET_MEMORY_COUNTER_out));
  Comparator comparator_1 (.a(INPUT_CHAR), .b({8{1'b0}}), .eq(comparator_1_eq));  // open: gt, lt
  not not_6 (not_6_out, PRND);
  Register #(.width(12)) register_4 (.D(adder_1_out), .Q(MEM_A), .clk(and_4_out), .clr(RES));  // open: en
  not not_7 (readConsole, PRND);
  and and_4 (and_4_out, not_6_out, clc);
  // UART uart_1: pin names not known; wires that end beside it: uart_1_p1, MEM_D, uart_1_p3, clc, uart_1_p3, CONNECTED, uart_1_p7
  Adder #(.width(12)) adder_1 (.a(MEM_A), .b(12'h1), .out(adder_1_out));  // open: cin, cout
  or or_3 (uart_1_p7, uart_1_p3, readConsole);
  Comparator #(.width(12)) comparator_2 (.a(MEM_A), .b(PRINT_SIZE), .eq(PRND));  // open: gt, lt

  // Notes on the sheet:
  //   12 бит адрес
  //   Frame Printed
  //   Print Frame
  //   A - Адрес к каторому обращается
  //   B - элемент по адресу
endmodule

// GE
module graphic_elems (
  input  [7:0] ADDR,
  input  [11:0] ELEM,
  output [7:0] DATA,
  output [11:0] LEN
);

  wire [7:0] deMux1, geD0, geD1, geD2, geD2_0, geD2_1, geD3, geD4, geD5, geD6, geD7, geD8, geD9, geD10,
       geD11, geD12, geD13, geD14, geD15;
  wire [11:0] deMuxl1;

  ROM #(.addrWidth(12)) rom_1 (.addr(ELEM), .data(geD0));  // open: sel
  ROM #(.addrWidth(12)) rom_2 (.addr(ELEM), .data(geD1));  // open: sel
  ROM #(.addrWidth(12)) rom_3 (.addr(ELEM), .data(geD2));  // open: sel
  ROM #(.addrWidth(12)) rom_4 (.addr(ELEM), .data(geD3));  // open: sel
  ROM #(.addrWidth(12)) rom_5 (.addr(ELEM), .data(geD4));  // open: sel
  ROM #(.addrWidth(12)) rom_6 (.addr(ELEM), .data(geD5));  // open: sel
  ROM #(.addrWidth(12)) rom_7 (.addr(ELEM), .data(geD6));  // open: sel
  ROM #(.addrWidth(12)) rom_8 (.addr(ELEM), .data(geD7));  // open: sel
  ROM #(.addrWidth(12)) rom_9 (.addr(ELEM), .data(geD8));  // open: sel
  ROM #(.addrWidth(12)) rom_10 (.addr(ELEM), .data(geD9));  // open: sel
  ROM #(.addrWidth(12)) rom_11 (.addr(ELEM), .data(geD10));  // open: sel
  ROM #(.addrWidth(12)) rom_12 (.addr(ELEM), .data(geD11));  // open: sel
  ROM #(.addrWidth(12)) rom_13 (.addr(ELEM), .data(geD12));  // open: sel
  ROM #(.addrWidth(12)) rom_14 (.addr(ELEM), .data(geD13));  // open: sel
  ROM #(.addrWidth(12)) rom_15 (.addr(ELEM), .data(geD14));  // open: sel
  ROM #(.addrWidth(12)) rom_16 (.addr(ELEM), .data(geD15));  // open: sel
  ROM #(.addrWidth(12)) rom_17 (.addr(ELEM), .data(geD2_0));  // open: sel
  ROM #(.addrWidth(12)) rom_18 (.addr(ELEM), .data(geD2_1));  // open: sel
  Multiplexer #(.select(5), .width(8), .enable("false")) multiplexer_1 (
    .in0(geD0), .in1(geD1), .in2(geD2), .in3(geD3), .in4(geD4), .in5(geD5), .in6(geD6), .in7(geD7),
    .in8(geD8), .in9(geD9), .in10(geD10), .in11(geD11), .in12(geD12), .in13(geD13), .in14(geD14),
    .in15(geD15), .in30(geD2_1), .in31(geD2_0), .out(deMux1), .sel(ADDR[4:0]));  // open: in16, in17, in18, in19, in20, in21, in22, in23, in24, in25, in26, in27, in28, in29
  Multiplexer #(.select(5), .width(12), .enable("false")) multiplexer_2 (
    .in0(12'had5), .in1(12'h596), .in2(12'h596), .in3(12'h596), .in4(12'h596), .in5(12'h596), .in6(12'h596),
    .in7(12'h596), .in8(12'h596), .in9(12'h596), .in10(12'h596), .in11(12'h596), .in12(12'h596),
    .in13(12'h596), .in14(12'h596), .in15(12'h596), .in30(12'had5), .in31(12'had5), .out(deMuxl1),
    .sel(ADDR[4:0]));  // open: in16, in17, in18, in19, in20, in21, in22, in23, in24, in25, in26, in27, in28, in29
  Multiplexer #(.select(3), .width(8), .enable("false")) multiplexer_3 (
    .in0(deMux1), .out(DATA), .sel(ADDR[7:5]));  // open: in1, in2, in3, in4, in5, in6, in7
  Multiplexer #(.select(3), .width(12), .enable("false")) multiplexer_4 (
    .in0(deMuxl1), .out(LEN), .sel(ADDR[7:5]));  // open: in1, in2, in3, in4, in5, in6, in7

  // Other names for the same wires on the sheet: geAddr1[4:0] = ADDR[4:0]; geAddr2[2:0] = ADDR[7:5];
  //   geEl[11:0] = ELEM

  // Notes on the sheet:
  //   BOARD
  //   contents of rom_1 (hex, n*v repeats v):
  //   0 76*23 a 23 52*20 23 21*20 23 a 23 52*20 23 21*20 23 a 23 52*20 23 21*20 23 a 23 52*20 23 21*20 23
  //   a 23 52*20 23 21*20 23 a 23 52*20 23 21*20 23 a 23 52*20 23 21*20 23 a 23 52*20 23 21*20 23 a 23
  //   52*20 23 21*20 23 a 23 52*20 23 21*20 23 a 23 52*20 23 21*20 23 a 23 52*20 23 21*20 23 a 23 52*20 23
  //   21*20 23 a 23 52*20 23 21*20 23 a 23 52*20 23 21*20 23 a 23 52*20 23 21*20 23 a 23 52*20 23 21*20 23
  //   a 23 52*20 23 21*20 23 a 23 52*20 23 21*20 23 a 23 52*20 23 21*20 23 a 23 52*20 23 21*20 23 a 23
  //   52*20 23*23 a 23 52*20 23 21*20 23 a 23 52*20 23 21*20 23 a 23 52*20 23 21*20 23 a 23 52*20 23 21*20
  //   23 a 23 52*20 23 21*20 23 a 76*23 a 23 74*20 23 a 76*23 a 23 9*20 23 9*20 23 9*20 23 9*20 23 9*20 23
  //   20 48 50 20 7c 10*20 7c 28 20 20 2f 35 30 29 20 23 a 23 9*20 23 9*20 23 9*20 23 9*20 23 9*20 23
  //   24*20 23 a 23 9*20 23 9*20 23 9*20 23 9*20 23 9*20 23 24*20 23 a 23 9*20 23 9*20 23 9*20 23 9*20 23
  //   9*20 23 24*20 23 a 76*23 a
  //   FFL
  //   contents of rom_2 (hex, n*v repeats v):
  //   0 51*20 a 52*20 a 52*20 a 9*20 34*5f 9*20 a 8*20 7c 34*23 7c 8*20 a 8*20 7c 34*23 7c 8*20 a 8*20 7c
  //   34*23 7c 8*20 a 8*20 7c 34*23 7c 8*20 a 8*20 7c 34*23 7c 8*20 a 8*20 7c 34*23 7c 8*20 a 8*20 7c
  //   34*23 7c 8*20 a 8*20 7c 34*23 7c 8*20 a 8*20 7c 34*23 7c 8*20 a 8*20 7c 34*23 7c 8*20 a 8*20 7c
  //   34*23 7c 8*20 a 8*20 7c 34*23 7c 8*20 a 8*20 7c 34*23 7c 8*20 a 8*20 7c 34*23 7c 8*20 a 8*20 7c
  //   34*23 7c 8*20 a 8*20 7c 34*23 7c 8*20 a 8*20 7c 34*23 7c 8*20 a 8*20 7c 34*23 7c 8*20 a 8*20 7c
  //   34*23 7c 8*20 a 52*20 a 52*20 a 52*20 a 52*20
  //   FFFL
  //   contents of rom_3 (hex, n*v repeats v):
  //   0 51*20 a 52*20 a 52*20 a 52*20 a 52*20 a 52*20 a 52*20 a 18*20 16*5f 18*20 a 17*20 7c 16*23 7c
  //   17*20 a 17*20 7c 16*23 7c 17*20 a 17*20 7c 16*23 7c 17*20 a 17*20 7c 16*23 7c 17*20 a 17*20 7c 16*23
  //   7c 17*20 a 17*20 7c 16*23 7c 17*20 a 17*20 7c 16*23 7c 17*20 a 17*20 7c 16*23 7c 17*20 a 17*20 7c
  //   16*23 7c 17*20 a 17*20 7c 16*23 7c 17*20 a 17*20 7c 16*23 7c 17*20 a 52*20 a 52*20 a 52*20 a 52*20 a
  //   52*20 a 52*20 a 52*20 a 52*20
  //   FFFFL
  //   contents of rom_4 (hex, n*v repeats v):
  //   0 51*20 a 52*20 a 52*20 a 52*20 a 52*20 a 52*20 a 52*20 a 52*20 a 52*20 a 52*20 a 24*20 4*5f 24*20 a
  //   23*20 7c 4*23 7c 23*20 a 23*20 7c 4*23 7c 23*20 a 23*20 7c 4*23 7c 23*20 a 23*20 7c 4*23 7c 23*20 a
  //   23*20 7c 4*23 7c 23*20 a 52*20 a 52*20 a 52*20 a 52*20 a 52*20 a 52*20 a 52*20 a 52*20 a 52*20 a
  //   52*20 a 52*20
  //   LFL
  //   contents of rom_5 (hex, n*v repeats v):
  //   0 5c 5f 49*20 a 23 23 5c 5f 48*20 a 4*23 5c 5f 46*20 a 6*23 5c 5f 44*20 a 8*23 7c 43*20 a 8*23 7c
  //   43*20 a 8*23 7c 43*20 a 8*23 7c 43*20 a 8*23 7c 43*20 a 8*23 7c 43*20 a 8*23 7c 43*20 a 8*23 7c
  //   43*20 a 8*23 7c 43*20 a 8*23 7c 43*20 a 8*23 7c 43*20 a 8*23 7c 43*20 a 8*23 7c 43*20 a 8*23 7c
  //   43*20 a 8*23 7c 43*20 a 8*23 7c 43*20 a 8*23 7c 43*20 a 8*23 7c 43*20 a 8*23 7c 43*20 a 6*23 2f
  //   45*20 a 4*23 2f 47*20 a 23 23 2f 49*20 a 2f 51*20
  //   LFFL
  //   contents of rom_6 (hex, n*v repeats v):
  //   0 51*20 a 52*20 a 52*20 a 8*5f 44*20 a 8*23 7c 43*20 a 8*23 7c 43*20 a 8*23 7c 43*20 a 8*23 7c 43*20
  //   a 8*23 7c 43*20 a 8*23 7c 43*20 a 8*23 7c 43*20 a 8*23 7c 43*20 a 8*23 7c 43*20 a 8*23 7c 43*20 a
  //   8*23 7c 43*20 a 8*23 7c 43*20 a 8*23 7c 43*20 a 8*23 7c 43*20 a 8*23 7c 43*20 a 8*23 7c 43*20 a 8*23
  //   7c 43*20 a 8*23 7c 43*20 a 8*23 7c 43*20 a 52*20 a 52*20 a 52*20 a 52*20
  //   LFFFL
  //   contents of rom_7 (hex, n*v repeats v):
  //   0 51*20 a 52*20 a 52*20 a 52*20 a 52*20 a 52*20 a 52*20 a 17*5f 35*20 a 17*23 7c 34*20 a 17*23 7c
  //   34*20 a 17*23 7c 34*20 a 17*23 7c 34*20 a 17*23 7c 34*20 a 17*23 7c 34*20 a 17*23 7c 34*20 a 17*23
  //   7c 34*20 a 17*23 7c 34*20 a 17*23 7c 34*20 a 17*23 7c 34*20 a 52*20 a 52*20 a 52*20 a 52*20 a 52*20
  //   a 52*20 a 52*20 a 52*20
  //   LFFFFL
  //   contents of rom_8 (hex, n*v repeats v):
  //   0 51*20 a 52*20 a 52*20 a 52*20 a 52*20 a 52*20 a 52*20 a 52*20 a 52*20 a 52*20 a 18*20 5*5f 29*20 a
  //   17*20 7c 5*23 7c 28*20 a 17*20 7c 5*23 7c 28*20 a 17*20 7c 5*23 7c 28*20 a 17*20 7c 5*23 7c 28*20 a
  //   17*20 7c 5*23 7c 28*20 a 52*20 a 52*20 a 52*20 a 52*20 a 52*20 a 52*20 a 52*20 a 52*20 a 52*20 a
  //   52*20 a 52*20
  //   RFL
  //   contents of rom_9 (hex, n*v repeats v):
  //   0 50*20 5f 2f a 48*20 5f 2f 23 23 a 46*20 5f 2f 4*23 a 44*20 5f 2f 6*23 a 43*20 7c 8*23 a 43*20 7c
  //   8*23 a 43*20 7c 8*23 a 43*20 7c 8*23 a 43*20 7c 8*23 a 43*20 7c 8*23 a 43*20 7c 8*23 a 43*20 7c 8*23
  //   a 43*20 7c 8*23 a 43*20 7c 8*23 a 43*20 7c 8*23 a 43*20 7c 8*23 a 43*20 7c 8*23 a 43*20 7c 8*23 a
  //   43*20 7c 8*23 a 43*20 7c 8*23 a 43*20 7c 8*23 a 43*20 7c 8*23 a 43*20 7c 8*23 a 45*20 5c 6*23 a
  //   47*20 5c 4*23 a 49*20 5c 23 23 a 51*20 5c
  //   RFFL
  //   contents of rom_10 (hex, n*v repeats v):
  //   0 51*20 a 52*20 a 52*20 a 52*20 a 41*20 5f 2f 7c 8*20 a 39*20 5f 2f 23 23 7c 8*20 a 37*20 5f 2f 4*23
  //   7c 8*20 a 35*20 5f 2f 6*23 7c 8*20 a 34*20 7c 8*23 7c 8*20 a 34*20 7c 8*23 7c 8*20 a 34*20 7c 8*23
  //   7c 8*20 a 34*20 7c 8*23 7c 8*20 a 34*20 7c 8*23 7c 8*20 a 34*20 7c 8*23 7c 8*20 a 34*20 7c 8*23 7c
  //   8*20 a 34*20 7c 8*23 7c 8*20 a 34*20 7c 8*23 7c 8*20 a 34*20 7c 8*23 7c 8*20 a 34*20 7c 8*23 7c 8*20
  //   a 36*20 5c 6*23 7c 8*20 a 38*20 5c 4*23 7c 8*20 a 40*20 5c 23 23 7c 8*20 a 42*20 5c 7c 8*20 a 52*20
  //   a 52*20 a 52*20 a 52*20
  //   RFFFL
  //   contents of rom_11 (hex, n*v repeats v):
  //   0 51*20 a 52*20 a 52*20 a 52*20 a 52*20 a 52*20 a 52*20 a 35*20 17*5f a 34*20 7c 17*23 a 34*20 7c
  //   17*23 a 34*20 7c 17*23 a 34*20 7c 17*23 a 34*20 7c 17*23 a 34*20 7c 17*23 a 34*20 7c 17*23 a 34*20
  //   7c 17*23 a 34*20 7c 17*23 a 34*20 7c 17*23 a 34*20 7c 17*23 a 52*20 a 52*20 a 52*20 a 52*20 a 52*20
  //   a 52*20 a 52*20 a 52*20
  //   RFFFFL
  //   contents of rom_12 (hex, n*v repeats v):
  //   0 51*20 a 52*20 a 52*20 a 52*20 a 52*20 a 52*20 a 52*20 a 52*20 a 52*20 a 52*20 a 29*20 5*5f 18*20 a
  //   28*20 7c 5*23 7c 17*20 a 28*20 7c 5*23 7c 17*20 a 28*20 7c 5*23 7c 17*20 a 28*20 7c 5*23 7c 17*20 a
  //   28*20 7c 5*23 7c 17*20 a 52*20 a 52*20 a 52*20 a 52*20 a 52*20 a 52*20 a 52*20 a 52*20 a 52*20 a
  //   52*20 a 52*20
  //   FRFL
  //   contents of rom_13 (hex, n*v repeats v):
  //   0 51*20 a 52*20 a 52*20 a 52*20 a 41*20 5f 2f 7c 8*20 a 39*20 5f 2f 23 23 7c 8*20 a 37*20 5f 2f 4*23
  //   7c 8*20 a 35*20 5f 2f 6*23 7c 8*20 a 34*20 7c 8*23 7c 8*20 a 34*20 7c 8*23 7c 8*20 a 34*20 7c 8*23
  //   7c 8*20 a 34*20 7c 8*23 7c 8*20 a 34*20 7c 8*23 7c 8*20 a 34*20 7c 8*23 7c 8*20 a 34*20 7c 8*23 7c
  //   8*20 a 34*20 7c 8*23 7c 8*20 a 34*20 7c 8*23 7c 8*20 a 34*20 7c 8*23 7c 8*20 a 34*20 7c 8*23 7c 8*20
  //   a 36*20 5c 6*23 7c 8*20 a 38*20 5c 4*23 7c 8*20 a 40*20 5c 23 23 7c 8*20 a 42*20 5c 7c 8*20 a 52*20
  //   a 52*20 a 52*20 a 52*20
  //   FLFL
  //   contents of rom_14 (hex, n*v repeats v):
  //   0 51*20 a 52*20 a 52*20 a 52*20 a 8*20 7c 5c 5f 41*20 a 8*20 7c 23 23 5c 5f 39*20 a 8*20 7c 4*23 5c
  //   5f 37*20 a 8*20 7c 6*23 5c 5f 35*20 a 8*20 7c 8*23 7c 34*20 a 8*20 7c 8*23 7c 34*20 a 8*20 7c 8*23
  //   7c 34*20 a 8*20 7c 8*23 7c 34*20 a 8*20 7c 8*23 7c 34*20 a 8*20 7c 8*23 7c 34*20 a 8*20 7c 8*23 7c
  //   34*20 a 8*20 7c 8*23 7c 34*20 a 8*20 7c 8*23 7c 34*20 a 8*20 7c 8*23 7c 34*20 a 8*20 7c 8*23 7c
  //   34*20 a 8*20 7c 6*23 2f 36*20 a 8*20 7c 4*23 2f 38*20 a 8*20 7c 23 23 2f 40*20 a 8*20 7c 2f 42*20 a
  //   52*20 a 52*20 a 52*20 a 52*20
  //   FFRFL
  //   contents of rom_15 (hex, n*v repeats v):
  //   0 51*20 a 52*20 a 52*20 a 52*20 a 52*20 a 52*20 a 52*20 a 52*20 a 32*20 5f 2f 7c 17*20 a 30*20 5f 2f
  //   23 23 7c 17*20 a 29*20 2f 4*23 7c 17*20 a 28*20 7c 5*23 7c 17*20 a 28*20 7c 5*23 7c 17*20 a 28*20 7c
  //   5*23 7c 17*20 a 28*20 7c 5*23 7c 17*20 a 28*20 7c 5*23 7c 17*20 a 29*20 5c 4*23 7c 17*20 a 31*20 5c
  //   23 23 7c 17*20 a 33*20 5c 7c 17*20 a 52*20 a 52*20 a 52*20 a 52*20 a 52*20 a 52*20 a 52*20 a 52*20
  //   FFLFL
  //   contents of rom_16 (hex, n*v repeats v):
  //   0 51*20 a 52*20 a 52*20 a 52*20 a 52*20 a 52*20 a 52*20 a 52*20 a 17*20 7c 5c 5f 32*20 a 17*20 7c 23
  //   23 5c 5f 30*20 a 17*20 7c 4*23 5c 29*20 a 17*20 7c 5*23 7c 28*20 a 17*20 7c 5*23 7c 28*20 a 17*20 7c
  //   5*23 7c 28*20 a 17*20 7c 5*23 7c 28*20 a 17*20 7c 5*23 7c 28*20 a 17*20 7c 4*23 2f 29*20 a 17*20 7c
  //   23 23 2f 31*20 a 17*20 7c 2f 33*20 a 52*20 a 52*20 a 52*20 a 52*20 a 52*20 a 52*20 a 52*20 a 52*20
  //   contents of rom_17 (hex, n*v repeats v):
  //   0 76*23 a 23 74*20 23 a 23 74*20 23 a 23 74*20 23 a 23 26*20 5*5f 20 20 5f 40*20 23 a 23 25*20 7c 5f
  //   20 20 20 5f 7c 7c 20 7c 39*20 23 a 23 27*20 7c 20 7c 20 20 7c 20 7c 5f 5f 4*20 5f 5f 5f 30*20 23 a
  //   23 27*20 7c 20 7c 20 20 7c 20 27 5f 20 5c 20 20 2f 20 5f 20 5c 29*20 23 a 23 27*20 7c 20 7c 20 20 7c
  //   20 7c 20 7c 20 7c 7c 20 20 5f 5f 2f 29*20 23 a 23 27*20 5c 5f 2f 20 20 7c 5f 7c 20 7c 5f 7c 20 5c 5f
  //   5f 5f 7c 29*20 23 a 23 20 5f 5f 5f 20 20 5f 5f 5f 8*20 5f 7*20 5f 7*20 5f 40*20 23 a 23 20 7c 20 20
  //   5c 2f 20 20 7c 7*20 7c 20 7c 5*20 28 20 29 5*20 7c 20 7c 39*20 23 a 23 20 7c 20 2e 20 20 2e 20 7c 20
  //   20 5f 5f 5f 20 20 7c 20 7c 20 20 5f 5f 5f 7c 2f 20 5f 5f 5f 20 20 7c 20 7c 5f 5f 20 20 20 5f 20 20
  //   20 5f 20 20 5f 20 5f 5f 20 20 5f 20 5f 5f 20 20 5f 5f 5f 20 5f 5f 6*20 5f 5f 20 23 a 23 20 7c 20 7c
  //   5c 2f 7c 20 7c 20 2f 20 5f 20 5c 20 7c 20 7c 20 2f 20 5f 20 5c 20 2f 20 5f 5f 7c 20 7c 20 27 5f 20
  //   5c 20 7c 20 7c 20 7c 20 7c 7c 20 27 5f 5f 7c 7c 20 27 5f 5f 7c 2f 20 5f 20 5c 5c 20 5c 20 2f 5c 20
  //   2f 20 2f 20 23 a 23 20 7c 20 7c 20 20 7c 20 7c 7c 20 28 5f 29 20 7c 7c 20 7c 7c 20 20 5f 5f 2f 20 5c
  //   5f 5f 20 5c 20 7c 20 7c 5f 29 20 7c 7c 20 7c 5f 7c 20 7c 7c 20 7c 20 20 20 7c 20 7c 20 20 7c 20 28
  //   5f 29 20 7c 5c 20 56 20 20 56 20 2f 20 20 23 a 23 20 5c 5f 7c 20 20 7c 5f 2f 20 5c 5f 5f 5f 2f 20 7c
  //   5f 7c 20 5c 5f 5f 5f 7c 20 7c 5f 5f 5f 2f 20 7c 5f 2e 5f 5f 2f 20 20 5c 5f 5f 2c 5f 7c 7c 5f 7c 20
  //   20 20 7c 5f 7c 20 20 20 5c 5f 5f 5f 2f 20 20 5c 5f 2f 5c 5f 2f 20 20 20 23 a 23 74*20 23 a 23 74*20
  //   23 a 23 74*20 23 a 23 74*20 23 a 23 74*20 23 a 23 74*20 23 a 23 74*20 23 a 23 74*20 23 a 23 74*20 23
  //   a 23 74*20 23 a 23 74*20 23 a 23 74*20 23 a 23 74*20 23 a 23 74*20 23 a 23 74*20 23 a 23 74*20 23 a
  //   23 74*20 23 a 23 39*20 50 52 45 53 53 20 41 4e 59 20 4b 45 59 20 54 4f 20 43 4f 4e 54 49 4e 55 45 2e
  //   2e 2e 7*20 23 a 23 74*20 23 a 76*23 a 52*20
  //   contents of rom_18 (hex, n*v repeats v):
  //   0 76*23 a 23 74*20 23 a 23 74*20 23 a 23 74*20 23 a 23 74*20 23 a 23 74*20 23 a 23 74*20 23 a 23
  //   74*20 23 a 23 74*20 23 a 23 6*20 7c 8*20 4d 6f 6c 65 8*20 7c 13*20 7c 20*20 7c 20 28 20 20 7c 20 20
  //   29 20 20 20 23 a 23 74*20 23 a 23 74*20 23 a 23 74*20 23 a 23 74*20 23 a 23 74*20 23 a 23 13*20 7b
  //   28 30 2d 30 29 7d 54*20 23 a 23 74*20 23 a 23 74*20 23 a 23 74*20 23 a 23 4*20 65*2d 5*20 23 a 23
  //   74*20 23 a 23 20*20 5e 24*20 2e 28*20 23 a 23 8*20 2e 19*20 2e 10*20 2e 18*20 2e 7*20 2e 7*20 23 a
  //   23 16*20 2e 17*20 2e 17*20 5e 7*20 2e 13*20 23 a 23 23*20 2e 18*20 2e 31*20 23 a 23 6*20 2e 6*20 5e
  //   16*20 5e 23*20 2e 19*20 23 a 23 23*20 2e 11*20 2e 5*20 2e 20*20 5e 11*20 23 a 23 74*20 23 a 76*23 a
  //   23 74*20 23 a 76*23 a 23 9*20 23 9*20 23 9*20 23 9*20 23 9*20 23 20 48 50 20 7c 10*20 7c 28 20 20 2f
  //   35 30 29 20 23 a 23 9*20 23 9*20 23 9*20 23 9*20 23 9*20 23 24*20 23 a 23 9*20 23 9*20 23 9*20 23
  //   9*20 23 9*20 23 24*20 23 a 23 9*20 23 9*20 23 9*20 23 9*20 23 9*20 23 24*20 23 a 76*23 a
  //   START SCREEN
  //   ATACK BOARD
endmodule

// Maps
module maps (
  input  [7:0] Map_No,
  input  [11:0] Addr_on_map,
  output [11:0] Width,
  output [11:0] Height,
  output [7:0] Xpp,
  output [7:0] Ypp,
  output [7:0] DATA,
  output [11:0] LEN
);

  wire [7:0] mgeD0, mgeD1, undriven_3, undriven_4;
  wire [11:0] undriven, undriven_2;

  ROM #(.addrWidth(12)) rom_1 (.addr(Addr_on_map), .data(mgeD1));  // open: sel
  ROM #(.addrWidth(12)) rom_2 (.addr(Addr_on_map), .data(mgeD0));  // open: sel
  Multiplexer #(.select(5), .width(8), .enable("false")) multiplexer_1 (
    .in0(mgeD0), .in1(mgeD1), .out(DATA), .sel(Map_No[4:0]));  // open: in2, in3, in4, in5, in6, in7, in8, in9, in10, in11, in12, in13, in14, in15, in16, in17, in18, in19, in20, in21, in22, in23, in24, in25, in26, in27, in28, in29, in30, in31
  Multiplexer #(.select(5), .width(12), .enable("false")) multiplexer_2 (
    .in0(12'h99), .out(LEN), .sel(Map_No[4:0]));  // open: in1, in2, in3, in4, in5, in6, in7, in8, in9, in10, in11, in12, in13, in14, in15, in16, in17, in18, in19, in20, in21, in22, in23, in24, in25, in26, in27, in28, in29, in30, in31
  Multiplexer #(.select(5), .width(12), .enable("false")) multiplexer_3 (
    .in0(12'hc), .in1(12'h9), .in30(undriven), .in31(undriven), .out(Width), .sel(Map_No[4:0]));  // open: in2, in3, in4, in5, in6, in7, in8, in9, in10, in11, in12, in13, in14, in15, in16, in17, in18, in19, in20, in21, in22, in23, in24, in25, in26, in27, in28, in29
  Multiplexer #(.select(5), .width(12), .enable("false")) multiplexer_4 (
    .in0(12'hc), .in1(12'h7), .in30(undriven_2), .in31(undriven_2), .out(Height), .sel(Map_No[4:0]));  // open: in2, in3, in4, in5, in6, in7, in8, in9, in10, in11, in12, in13, in14, in15, in16, in17, in18, in19, in20, in21, in22, in23, in24, in25, in26, in27, in28, in29
  Multiplexer #(.select(5), .width(8), .enable("false")) multiplexer_5 (
    .in0(8'h5), .in1(8'h3), .in30(undriven_3), .in31(undriven_3), .out(Xpp), .sel(Map_No[4:0]));  // open: in2, in3, in4, in5, in6, in7, in8, in9, in10, in11, in12, in13, in14, in15, in16, in17, in18, in19, in20, in21, in22, in23, in24, in25, in26, in27, in28, in29
  Multiplexer #(.select(5), .width(8), .enable("false")) multiplexer_6 (
    .in0(8'h5), .in1(8'h2), .in30(undriven_4), .in31(undriven_4), .out(Ypp), .sel(Map_No[4:0]));  // open: in2, in3, in4, in5, in6, in7, in8, in9, in10, in11, in12, in13, in14, in15, in16, in17, in18, in19, in20, in21, in22, in23, in24, in25, in26, in27, in28, in29

  // Other names for the same wires on the sheet: map_char[7:0] = DATA; mgeAddr1[4:0] = Map_No[4:0];
  //   mdeMuxl1[11:0] = LEN; mgeEl[11:0] = Addr_on_map

  // Notes on the sheet:
  //   TEST MAP
  //   contents of rom_1 (hex, n*v repeats v):
  //   0 4 3 2 36*23 20 66 6a 61 20 6*23 20 23 23 20 32 6*23 20 20 23 23 20 36*23
  //   contents of rom_2 (hex, n*v repeats v):
  //   40*23 20 23 20 20 20 7*23 20 23 20 23 20 6*23 4*20 23 20 6*23 20 23 4*20 6*23 20 23 23 20 8*23 20 20
  //   23 20 20 20 39*23
endmodule

module printing_map (
  input  [7:0] No_of_map,
  input  [7:0] Xpp,
  input  [7:0] Ypp,
  input  Clock,
  input  [1:0] Direction,
  input  [7:0] Num_of_elem,
  input  [11:0] Mem_N,
  input  Main_Res,
  output [7:0] Char_on_screen,
  output Cond_of_change
);

  wire and_3_out, comparator_1_eq, comparator_2_eq, comparator_3_lt, comparator_4_lt, comparator_5_gt,
       comparator_6_eq, Cond_next_str_mMap, mole_s_sprite_on_map_1_cond_of_change, not_1_out, not_2_out,
       or_1_out, or_2_out, partition_on_sections_1_condition_of_writing;
  wire [4:0] adder_13_out, register_2_q;
  wire [7:0] maps_1_data, maps_2_data, maps_3_data, maps_4_data, maps_5_data, maps_6_data, maps_7_data,
       mole_s_sprite_on_map_1_out_char, multiplexer_1_out;
  wire [11:0] adder_1_out, adder_2_out, adder_3_out, adder_4_out, addr, Height, Mem_Rem, multiplier_1_out,
       num1, num2, num3, num4, num5, num6, num7, Num_of_str_on_map, Width;

  Register #(.width(12)) register_1 (
    .D(adder_2_out), .Q(Num_of_str_on_map), .clk(Cond_next_str_mMap), .clr(Main_Res));  // open: en
  Adder #(.width(12)) adder_1 (.a(12'hffd), .b(Num_of_str_on_map), .out(adder_1_out));  // open: cin, cout
  Adder #(.width(12)) adder_2 (.a(Num_of_str_on_map), .b(12'h1), .out(adder_2_out));  // open: cin, cout
  Comparator #(.mode("unsigned")) comparator_1 (.a(Num_of_elem), .b({8{1'b0}}), .eq(comparator_1_eq));  // open: gt, lt
  Adder #(.width(12)) adder_3 (.a({4'b0000, Ypp}), .b(adder_1_out), .out(adder_3_out));  // open: cin, cout
  Divider #(.width(12)) divider_1 (.a(Mem_N), .b(12'he7), .rem(Mem_Rem));  // open: out, upper
  Comparator #(.width(12), .mode("unsigned")) comparator_2 (
    .a(Mem_Rem), .b(12'h83), .eq(comparator_2_eq));  // open: gt, lt
  Comparator #(.width(12), .mode("unsigned")) comparator_3 (
    .a(Mem_N), .b(12'h6b2), .lt(comparator_3_lt));  // open: gt, eq
  Comparator #(.width(12), .mode("unsigned")) comparator_4 (
    .a(Mem_N), .b(12'h84), .lt(comparator_4_lt));  // open: gt, eq
  Comparator #(.width(12), .mode("unsigned")) comparator_5 (
    .a(Mem_N), .b(12'h85), .gt(comparator_5_gt));  // open: eq, lt
  Multiplier #(.width(12)) multiplier_1 (.a(Width), .b(adder_3_out), .out(multiplier_1_out));  // open: cin, cout
  // Probe on multiplier_1_out
  and and_1 (Cond_next_str_mMap, comparator_1_eq, comparator_2_eq, comparator_5_gt, comparator_3_lt);
  not not_1 (not_1_out, comparator_4_lt);
  Adder #(.width(12)) adder_4 (.a({4'b0000, Xpp}), .b(12'hffd), .out(adder_4_out));  // open: cin, cout
  Adder #(.width(12)) adder_5 (.a(adder_4_out), .b(multiplier_1_out), .out(addr));  // open: cin, cout
  partition_on_sections partition_on_sections_1 (
    .Reminder(Mem_Rem), .Condition_of_writing(partition_on_sections_1_condition_of_writing));
  and and_2 (Cond_of_change, partition_on_sections_1_condition_of_writing, not_1_out, comparator_1_eq, comparator_3_lt);
  Adder #(.width(12)) adder_6 (.a(addr), .b({12{1'b0}}), .out(num1));  // open: cin, cout
  Adder #(.width(12)) adder_7 (.a(addr), .b(12'h1), .out(num2));  // open: cin, cout
  Adder #(.width(12)) adder_8 (.a(addr), .b(12'h2), .out(num3));  // open: cin, cout
  Adder #(.width(12)) adder_9 (.a(addr), .b(12'h3), .out(num4));  // open: cin, cout
  Adder #(.width(12)) adder_10 (.a(addr), .b(12'h4), .out(num5));  // open: cin, cout
  Adder #(.width(12)) adder_11 (.a(addr), .b(12'h5), .out(num6));  // open: cin, cout
  Adder #(.width(12)) adder_12 (.a(addr), .b(12'h6), .out(num7));  // open: cin, cout
  // Probe on num1
  // Probe on num2
  // Probe on num3
  // Probe on num4
  // Probe on num5
  // Probe on num6
  // Probe on num7
  maps maps_1 (
    .Map_No(No_of_map), .Addr_on_map(num1), .Width(Width), .Height(Height), .DATA(maps_1_data));  // open: Xpp, Ypp, LEN
  maps maps_2 (.Map_No(No_of_map), .Addr_on_map(num2), .DATA(maps_2_data));  // open: Width, Height, Xpp, Ypp, LEN
  maps maps_3 (.Map_No(No_of_map), .Addr_on_map(num3), .DATA(maps_3_data));  // open: Width, Height, Xpp, Ypp, LEN
  maps maps_4 (.Map_No(No_of_map), .Addr_on_map(num4), .DATA(maps_4_data));  // open: Width, Height, Xpp, Ypp, LEN
  maps maps_5 (.Map_No(No_of_map), .Addr_on_map(num5), .DATA(maps_5_data));  // open: Width, Height, Xpp, Ypp, LEN
  maps maps_6 (.Map_No(No_of_map), .Addr_on_map(num6), .DATA(maps_6_data));  // open: Width, Height, Xpp, Ypp, LEN
  maps maps_7 (.Map_No(No_of_map), .Addr_on_map(num7), .DATA(maps_7_data));  // open: Width, Height, Xpp, Ypp, LEN
  // Probe on maps_1_data
  // Probe on maps_2_data
  // Probe on maps_3_data
  // Probe on maps_4_data
  // Probe on maps_5_data
  // Probe on maps_6_data
  // Probe on maps_7_data
  Multiplexer #(.select(5), .width(8)) multiplexer_1 (
    .in1(maps_1_data), .in2(maps_1_data), .in3(maps_1_data), .in4(maps_2_data), .in5(maps_2_data),
    .in6(maps_2_data), .in7(maps_3_data), .in8(maps_3_data), .in9(maps_3_data), .in10(maps_4_data),
    .in11(maps_4_data), .in12(maps_4_data), .in13(maps_5_data), .in14(maps_5_data), .in15(maps_5_data),
    .in16(maps_6_data), .in17(maps_6_data), .in18(maps_6_data), .in19(maps_7_data), .in20(maps_7_data),
    .in21(maps_7_data), .out(multiplexer_1_out), .sel(register_2_q));  // open: in0, in22, in23, in24, in25, in26, in27, in28, in29, in30, in31, en
  // Probe on register_2_q
  Register #(.width(5)) register_2 (.D(adder_13_out), .Q(register_2_q), .clk(and_3_out), .clr(or_1_out));  // open: en
  and and_3 (and_3_out, Cond_of_change, Clock);
  or or_1 (or_1_out, Main_Res, comparator_6_eq);
  Mole_s_sprite_on_map mole_s_sprite_on_map_1 (
    .reminder(Mem_Rem), .Num_of_str_on_map(Num_of_str_on_map), .Direction(Direction), .Clock(Clock),
    .Reset_Str(or_2_out), .Cond_of_change(mole_s_sprite_on_map_1_cond_of_change),
    .Out_char(mole_s_sprite_on_map_1_out_char));
  or or_2 (or_2_out, Cond_next_str_mMap, Main_Res);
  Adder #(.width(5)) adder_13 (.a(register_2_q), .b(5'b00001), .out(adder_13_out));  // open: cin, cout
  assign Char_on_screen = mole_s_sprite_on_map_1_cond_of_change ? mole_s_sprite_on_map_1_out_char : 8'bz;  // Controlled_Buffer controlled_buffer_1
  not not_2 (not_2_out, mole_s_sprite_on_map_1_cond_of_change);
  assign Char_on_screen = not_2_out ? multiplexer_1_out : 8'bz;  // Controlled_Buffer controlled_buffer_2
  Comparator #(.width(5), .mode("unsigned")) comparator_6 (
    .a(5'b10110), .b(register_2_q), .eq(comparator_6_eq));  // open: gt, lt

  // Other names for the same wires on the sheet: Direct[1:0] = Direction; No[7:0] = No_of_map; Res = Main_Res
endmodule

module x_y__to_memory_elem_number (
  input  [11:0] H,
  input  [7:0] Y,
  input  [7:0] X,
  input  [11:0] START,
  output [11:0] ELEM
);

  wire [11:0] adder_1_out, bit_extender_1_out, bit_extender_2_out, multiplier_1_out;

  assign bit_extender_1_out = {{4{1'b0}}, Y};  // Bit_Extender bit_extender_1
  Multiplier #(.width(12)) multiplier_1 (.a(H), .b(bit_extender_1_out), .out(multiplier_1_out));  // open: cin, cout
  assign bit_extender_2_out = {{4{1'b0}}, X};  // Bit_Extender bit_extender_2
  Adder #(.width(12)) adder_1 (.a(multiplier_1_out), .b(bit_extender_2_out), .out(adder_1_out));  // open: cin, cout
  Adder #(.width(12)) adder_2 (.a(adder_1_out), .b(START), .out(ELEM));  // open: cin, cout
endmodule

module enemies (
  input  [1:0] ADDR,
  input  [7:0] ELEMIm,
  input  [7:0] ELEMNm,
  output [7:0] Img,
  output [7:0] Txt,
  output [7:0] HP,
  output [7:0] DMG
);

  wire [7:0] EnImEl1, EnImEl1txt, EnImEl2, EnImEl2txt, EnImEl3, EnImEl3txt, EnImEl4, EnImEl4txt;

  ROM rom_1 (.addr(ELEMIm), .data(EnImEl1));  // open: sel
  ROM rom_2 (.addr(ELEMIm), .data(EnImEl2));  // open: sel
  ROM rom_3 (.addr(ELEMIm), .data(EnImEl3));  // open: sel
  ROM rom_4 (.addr(ELEMIm), .data(EnImEl4));  // open: sel
  Multiplexer #(.select(2), .width(8), .enable("false")) multiplexer_1 (
    .in0(EnImEl1), .in1(EnImEl2), .in2(EnImEl3), .in3(EnImEl4), .out(Img), .sel(ADDR));
  Multiplexer #(.select(2), .width(8), .enable("false")) multiplexer_2 (
    .in0(EnImEl1txt), .in1(EnImEl2txt), .in2(EnImEl3txt), .in3(EnImEl4txt), .out(Txt), .sel(ADDR));
  Multiplexer #(.select(2), .width(8), .disabled(0), .enable("false")) multiplexer_3 (
    .in0(8'h14), .in1(8'ha), .in2(8'h32), .in3(8'h1e), .out(HP), .sel(ADDR));
  Multiplexer #(.select(2), .width(8), .disabled(0), .enable("false")) multiplexer_4 (
    .in0(8'h5), .in1(8'h3), .in2(8'h14), .in3(8'ha), .out(DMG), .sel(ADDR));
  ROM rom_5 (.addr(ELEMIm), .data(EnImEl1txt));  // open: sel
  ROM rom_6 (.addr(ELEMIm), .data(EnImEl2txt));  // open: sel
  ROM rom_7 (.addr(ELEMIm), .data(EnImEl3txt));  // open: sel
  ROM rom_8 (.addr(ELEMIm), .data(EnImEl4txt));  // open: sel

  // Other names for the same wires on the sheet: enaddr1[1:0] = ADDR; EnImEl[7:0] = ELEMIm; EnImEltxt[7:0] = ELEMNm

  // Notes on the sheet:
  //   rat
  //   mouse
  //   ferret
  //   snake
  //   contents of rom_1 (hex, n*v repeats v):
  //   15*20 35 64 6d 67 2e 9*20 2f 5c 5f 2f 5c 16*20 28 20 6f 20 6f 20 29 15*20 2f 20 20 56 20 20 5c 15*20
  //   2f 20 3e 20 20 3c 20 20 5c 12*20 28 20 2f 5*20 5c 20 29 20 20 20 7c 8*20 5c 5f 20 4*2d 20 5f 2f 5f
  //   5f 5f 2f 24*20
  //   contents of rom_2 (hex, n*v repeats v):
  //   13*20 33 64 6d 67 2e 13*20 2f 5e 5c 5e 5c 5f 10*20 2f 4*20 7c 5*20 6f 5c 5f 7*20 7c 4*20 2f 7*20 5f
  //   2f 7*20 5c 20 20 20 2f 6*20 5f 5f 3e 9*20 5c 5f 5f 7c 20 20 20 5f 5f 5f 29 14*20 5c 5f 5f 5f 7c 5c
  //   5f 5f 30*20
  //   contents of rom_3 (hex, n*v repeats v):
  //   14*20 32 30 64 6d 67 2e 8*20 2f 29 5*5f 28 5c 12*20 28 2f 20 6f 20 20 20 6f 20 5c 29 11*20 7c 4*20
  //   4f 4*20 7c 12*20 5c 20 20 2d 5e 2d 20 20 2f 13*20 2f 7*20 5c 12*20 7c 9*20 7c 28*20
  //   contents of rom_4 (hex, n*v repeats v):
  //   14*20 31 30 64 6d 67 2e 4*20 2e 2d 2e 17*20 3e 2d 30 5f 30 29 29 20 20 7c 20 20 2f 20 29 11*20 2f 2f
  //   20 20 20 7c 2e 2f 5f 5f 29 10*20 28 28 5f 2e 2d 2d 27 20 5f 20 20 27 2e 10*20 60 2d 5f 5f 2d 2d 27
  //   20 27 2d 2e 20 29 16*20 5f 5f 2d 2d 27 28*20
  //   rat
  //   mouse
  //   ferret
  //   snake
  //   8x22 = 176
  //   20 chars name len
  //   contents of rom_5 (hex, n*v repeats v):
  //   6*20 53 43 41 52 59 20 52 41 54 5*20
  //   contents of rom_6 (hex, n*v repeats v):
  //   5*20 45 56 49 4c 20 4d 4f 55 53 45 5*20
  //   contents of rom_7 (hex, n*v repeats v):
  //   4*20 43 55 54 45 20 46 45 52 52 45 54 5*20
  //   contents of rom_8 (hex, n*v repeats v):
  //   4*20 4c 49 54 54 4c 45 20 53 4e 41 4b 45 4*20
endmodule

module quick (
  input  IN,
  output OUT
);

  wire not_1_out, not_2_out;

  not not_1 (not_1_out, IN);
  Register #(.width(1)) register_1 (.D(IN), .Q(OUT), .clk(IN), .clr(not_2_out));  // open: en
  not not_2 (not_2_out, not_1_out);
endmodule

module food (
  input  [7:0] FOOD,
  output [7:0] GIVEHP
);

  wire [1:0] bit_extender_1_out;
  wire [7:0] subtractor_1_out;

  Subtractor subtractor_1 (.a(FOOD), .b(8'h61), .out(subtractor_1_out));  // open: bin, bout
  Multiplexer #(.select(2), .width(8), .enable("false")) multiplexer_1 (
    .in0(8'h5), .in1(8'h3), .in2(8'h7), .in3(8'ha), .out(GIVEHP), .sel(bit_extender_1_out));
  Bit_Extender #(.out_width(2)) bit_extender_1 (.in(subtractor_1_out), .out(bit_extender_1_out));

  // Notes on the sheet:
  //   const/2
endmodule

module Lquick (
  input  IN,
  input  CLC,
  output OUT
);

  wire and_1_out, comparator_1_eq, quick_1_out;
  wire [2:0] adder_1_out, register_1_q;

  and and_1 (and_1_out, CLC, ~comparator_1_eq);  // AND_Gate
  quick quick_1 (.IN(IN), .OUT(quick_1_out));
  Adder #(.width(3)) adder_1 (.a(3'b001), .b(register_1_q), .out(adder_1_out));  // open: cin, cout
  Comparator #(.width(3), .mode("unsigned")) comparator_1 (
    .a(3'b111), .b(register_1_q), .gt(OUT), .eq(comparator_1_eq));  // open: lt
  Register #(.width(3)) register_1 (.D(adder_1_out), .Q(register_1_q), .clk(and_1_out), .clr(quick_1_out));  // open: en
endmodule

module weapon (
  input  GenRnd,
  input  [7:0] WEAPON,
  output [7:0] DMG
);

  wire random_1_out;
  wire [2:0] bit_extender_1_out;
  wire [7:0] bit_extender_2_out, multiplexer_1_out, subtractor_1_out;

  Subtractor subtractor_1 (.a(WEAPON), .b(8'h66), .out(subtractor_1_out));  // open: bin, bout
  Multiplexer #(.select(3), .width(8), .enable("false")) multiplexer_1 (
    .in0(8'h5), .in1(8'h14), .in2(8'hf), .in3(8'ha), .in4({8{1'b1}}), .out(multiplexer_1_out),
    .sel(bit_extender_1_out));  // open: in5, in6, in7
  Bit_Extender #(.out_width(3)) bit_extender_1 (.in(subtractor_1_out), .out(bit_extender_1_out));
  assign bit_extender_2_out = {{7{1'b0}}, random_1_out};  // Bit_Extender bit_extender_2
  Random #(.width(1)) random_1 (.clk(GenRnd), .out(random_1_out));  // open: next, clr
  Adder adder_1 (.a(bit_extender_2_out), .b(multiplexer_1_out), .out(DMG));  // open: cin, cout
endmodule

module partition_on_sections (
  input  [11:0] Reminder,
  output Condition_of_writing
);

  wire and_1_out, and_2_out, and_3_out, comparator_1_lt, comparator_2_gt, comparator_3_lt, comparator_4_gt,
       comparator_5_lt, comparator_6_gt, not_1_out, not_2_out, not_3_out, not_4_out, not_5_out, not_6_out;
  wire [11:0] adder_1_out;

  Adder #(.width(12)) adder_1 (.a(Reminder), .b({12{1'b0}}), .out(adder_1_out));  // open: cin, cout
  // Probe on adder_1_out
  Comparator #(.width(12), .mode("unsigned")) comparator_1 (
    .a(adder_1_out), .b(12'h84), .lt(comparator_1_lt));  // open: gt, eq
  Comparator #(.width(12), .mode("unsigned")) comparator_2 (
    .a(adder_1_out), .b(12'h98), .gt(comparator_2_gt));  // open: eq, lt
  Comparator #(.width(12), .mode("unsigned")) comparator_3 (
    .a(adder_1_out), .b(12'hd1), .lt(comparator_3_lt));  // open: gt, eq
  Comparator #(.width(12), .mode("unsigned")) comparator_4 (
    .a(adder_1_out), .b(12'he5), .gt(comparator_4_gt));  // open: eq, lt
  Comparator #(.width(12), .mode("unsigned")) comparator_5 (
    .a(adder_1_out), .b(12'h37), .lt(comparator_5_lt));  // open: gt, eq
  Comparator #(.width(12), .mode("unsigned")) comparator_6 (
    .a(adder_1_out), .b(12'h4b), .gt(comparator_6_gt));  // open: eq, lt
  not not_1 (not_1_out, comparator_1_lt);
  not not_2 (not_2_out, comparator_2_gt);
  not not_3 (not_3_out, comparator_3_lt);
  not not_4 (not_4_out, comparator_4_gt);
  not not_5 (not_5_out, comparator_5_lt);
  not not_6 (not_6_out, comparator_6_gt);
  and and_1 (and_1_out, not_1_out, not_2_out);
  or or_1 (Condition_of_writing, and_1_out, and_2_out, and_3_out);
  and and_2 (and_2_out, not_3_out, not_4_out);
  and and_3 (and_3_out, not_5_out, not_6_out);
endmodule

module Mole_s_sprite_on_map (
  input  [11:0] reminder,
  input  Clock,
  input  Reset_Str,
  input  [11:0] Num_of_str_on_map,
  input  [1:0] Direction,
  output Cond_of_change,
  output [7:0] Out_char
);

  wire _1_sect, _2_sect, _3_sect, and_4_out, and_6_out, and_7_out, and_8_out, and_9_out, and_10_out,
       and_11_out, and_12_out, and_13_out, and_14_out, and_15_out, and_16_out, and_17_out, comparator_5_lt,
       comparator_6_gt, comparator_7_lt, comparator_8_gt, comparator_9_lt, comparator_10_gt,
       comparator_11_eq, Dir_0, Dir_1, Dir_2, Dir_3, not_1_out, not_2_out, not_3_out, not_4_out, not_5_out,
       not_6_out, or_1_out;
  wire [1:0] adder_1_out, register_1_q;
  wire [7:0] rom_1_data, rom_2_data, rom_3_data, rom_4_data, rom_5_data, rom_6_data, rom_7_data, rom_8_data,
       rom_9_data, rom_10_data, rom_11_data, rom_12_data;

  Comparator #(.width(2), .mode("unsigned")) comparator_1 (.a(Direction), .b(2'b00), .eq(Dir_0));  // open: gt, lt
  Comparator #(.width(2), .mode("unsigned")) comparator_2 (.a(Direction), .b(2'b01), .eq(Dir_1));  // open: gt, lt
  Comparator #(.width(2), .mode("unsigned")) comparator_3 (.a(Direction), .b(2'b10), .eq(Dir_2));  // open: gt, lt
  Comparator #(.width(2), .mode("unsigned")) comparator_4 (.a(Direction), .b(2'b11), .eq(Dir_3));  // open: gt, lt
  Comparator #(.width(12), .mode("unsigned")) comparator_5 (
    .a(reminder), .b(12'h8d), .lt(comparator_5_lt));  // open: gt, eq
  not not_1 (not_1_out, comparator_5_lt);
  not not_2 (not_2_out, comparator_6_gt);
  Comparator #(.width(12), .mode("unsigned")) comparator_6 (
    .a(reminder), .b(12'h8f), .gt(comparator_6_gt));  // open: eq, lt
  Comparator #(.width(12), .mode("unsigned")) comparator_7 (
    .a(reminder), .b(12'hda), .lt(comparator_7_lt));  // open: gt, eq
  not not_3 (not_3_out, comparator_7_lt);
  not not_4 (not_4_out, comparator_8_gt);
  Comparator #(.width(12), .mode("unsigned")) comparator_8 (
    .a(reminder), .b(12'hdc), .gt(comparator_8_gt));  // open: eq, lt
  Comparator #(.width(12), .mode("unsigned")) comparator_9 (
    .a(reminder), .b(12'h40), .lt(comparator_9_lt));  // open: gt, eq
  not not_5 (not_5_out, comparator_9_lt);
  not not_6 (not_6_out, comparator_10_gt);
  Comparator #(.width(12), .mode("unsigned")) comparator_10 (
    .a(reminder), .b(12'h42), .gt(comparator_10_gt));  // open: eq, lt
  Comparator #(.width(12), .mode("unsigned")) comparator_11 (
    .a(Num_of_str_on_map), .b(12'h3), .eq(comparator_11_eq));  // open: gt, lt
  and and_1 (_1_sect, not_1_out, not_2_out);
  and and_2 (_2_sect, not_3_out, not_4_out);
  and and_3 (_3_sect, not_5_out, not_6_out);
  Register #(.width(2)) register_1 (.D(adder_1_out), .Q(register_1_q), .clk(and_4_out), .clr(Reset_Str));  // open: en
  and and_4 (and_4_out, or_1_out, comparator_11_eq, Clock);
  or or_1 (or_1_out, _1_sect, _2_sect, _3_sect);
  Adder #(.width(2)) adder_1 (.a(register_1_q), .b(2'b01), .out(adder_1_out));  // open: cin, cout
  and and_5 (Cond_of_change, or_1_out, comparator_11_eq);
  ROM #(.addrWidth(2)) rom_1 (.addr(register_1_q), .data(rom_1_data));  // open: sel
  ROM #(.addrWidth(2)) rom_2 (.addr(register_1_q), .data(rom_2_data));  // open: sel
  ROM #(.addrWidth(2)) rom_3 (.addr(register_1_q), .data(rom_3_data));  // open: sel
  ROM #(.addrWidth(2)) rom_4 (.addr(register_1_q), .data(rom_4_data));  // open: sel
  ROM #(.addrWidth(2)) rom_5 (.addr(register_1_q), .data(rom_5_data));  // open: sel
  ROM #(.addrWidth(2)) rom_6 (.addr(register_1_q), .data(rom_6_data));  // open: sel
  ROM #(.addrWidth(2)) rom_7 (.addr(register_1_q), .data(rom_7_data));  // open: sel
  ROM #(.addrWidth(2)) rom_8 (.addr(register_1_q), .data(rom_8_data));  // open: sel
  ROM #(.addrWidth(2)) rom_9 (.addr(register_1_q), .data(rom_9_data));  // open: sel
  ROM #(.addrWidth(2)) rom_10 (.addr(register_1_q), .data(rom_10_data));  // open: sel
  ROM #(.addrWidth(2)) rom_11 (.addr(register_1_q), .data(rom_11_data));  // open: sel
  ROM #(.addrWidth(2)) rom_12 (.addr(register_1_q), .data(rom_12_data));  // open: sel
  and and_6 (and_6_out, _1_sect, Dir_0);
  assign Out_char = and_6_out ? rom_1_data : 8'bz;  // Controlled_Buffer controlled_buffer_1
  and and_7 (and_7_out, _2_sect, Dir_0);
  assign Out_char = and_7_out ? rom_2_data : 8'bz;  // Controlled_Buffer controlled_buffer_2
  and and_8 (and_8_out, _3_sect, Dir_0);
  assign Out_char = and_8_out ? rom_3_data : 8'bz;  // Controlled_Buffer controlled_buffer_3
  and and_9 (and_9_out, _1_sect, Dir_1);
  assign Out_char = and_9_out ? rom_4_data : 8'bz;  // Controlled_Buffer controlled_buffer_4
  and and_10 (and_10_out, _2_sect, Dir_1);
  assign Out_char = and_10_out ? rom_5_data : 8'bz;  // Controlled_Buffer controlled_buffer_5
  and and_11 (and_11_out, _3_sect, Dir_1);
  assign Out_char = and_11_out ? rom_6_data : 8'bz;  // Controlled_Buffer controlled_buffer_6
  and and_12 (and_12_out, _1_sect, Dir_2);
  assign Out_char = and_12_out ? rom_7_data : 8'bz;  // Controlled_Buffer controlled_buffer_7
  and and_13 (and_13_out, _2_sect, Dir_2);
  assign Out_char = and_13_out ? rom_8_data : 8'bz;  // Controlled_Buffer controlled_buffer_8
  and and_14 (and_14_out, _3_sect, Dir_2);
  assign Out_char = and_14_out ? rom_9_data : 8'bz;  // Controlled_Buffer controlled_buffer_9
  and and_15 (and_15_out, _1_sect, Dir_3);
  assign Out_char = and_15_out ? rom_10_data : 8'bz;  // Controlled_Buffer controlled_buffer_10
  and and_16 (and_16_out, _2_sect, Dir_3);
  assign Out_char = and_16_out ? rom_11_data : 8'bz;  // Controlled_Buffer controlled_buffer_11
  and and_17 (and_17_out, _3_sect, Dir_3);
  assign Out_char = and_17_out ? rom_12_data : 8'bz;  // Controlled_Buffer controlled_buffer_12

  // Notes on the sheet:
  //   Direction 0
  //   Direction 1
  //   Direction 2
  //   Direction 3
  //   contents of rom_1 (hex, n*v repeats v):
  //   0 27 20 27
  //   contents of rom_2 (hex, n*v repeats v):
  //   0 5b 23 5d
  //   contents of rom_3 (hex, n*v repeats v):
  //   0 4a 20 4c
  //   contents of rom_4 (hex, n*v repeats v):
  //   0 20 2c 2c
  //   contents of rom_5 (hex, n*v repeats v):
  //   0 5b 7d 2d
  //   contents of rom_6 (hex, n*v repeats v):
  //   0 4a 4c 20
  //   contents of rom_7 (hex, n*v repeats v):
  //   0 5f 20 5f
  //   contents of rom_8 (hex, n*v repeats v):
  //   0 7b 23 7d
  //   contents of rom_9 (hex, n*v repeats v):
  //   0 4a 20 4c
  //   contents of rom_10 (hex, n*v repeats v):
  //   0 2c 2c 20
  //   contents of rom_11 (hex, n*v repeats v):
  //   0 2d 7b 5d
  //   contents of rom_12 (hex, n*v repeats v):
  //   0 20 4a 4c
endmodule

module Mole_s_Sprites_on_board (
  input  [7:0] Num_of_elem,
  input  [11:0] Mem_N,
  output Cond_of_change
);

  wire comparator_1_eq;

  Comparator comparator_1 (.a(Num_of_elem), .b({8{1'b0}}), .eq(comparator_1_eq));  // open: gt, lt
  ROM #(.addrWidth(7)) rom_1 ();  // open: addr, data, sel
endmodule
